// Logisim project 4bit_sort.circ as structural Verilog: 4 circuits, main circuit 1bit_swap
module _1bit_swap (
  input  in_1,
  input  in_2,
  input  in_3,
  output out_4,
  output out_5
);

  wire not_1_out, not_2_out;

  assign out_4 = not_1_out ? in_1 : 1'bz;  // Controlled_Buffer controlled_buffer_1
  not not_1 (not_1_out, in_3);
  assign out_5 = not_2_out ? in_2 : 1'bz;  // Controlled_Buffer controlled_buffer_2
  not not_2 (not_2_out, in_3);
  assign out_4 = in_3 ? in_2 : 1'bz;  // Controlled_Buffer controlled_buffer_3
  assign out_5 = in_3 ? in_1 : 1'bz;  // Controlled_Buffer controlled_buffer_4
endmodule

module _4bit_swap (
  input  [3:0] in_1,
  input  [3:0] in_2,
  input  in_3,
  output [3:0] out_4,
  output [3:0] out_5
);

  wire not_1_out;

  not not_1 (not_1_out, in_3);
  assign out_4 = not_1_out ? in_1 : 4'bz;  // Controlled_Buffer controlled_buffer_1
  assign out_5 = not_1_out ? in_2 : 4'bz;  // Controlled_Buffer controlled_buffer_2
  assign out_4 = in_3 ? in_2 : 4'bz;  // Controlled_Buffer controlled_buffer_3
  assign out_5 = in_3 ? in_1 : 4'bz;  // Controlled_Buffer controlled_buffer_4
endmodule

module _4bit_sort (
  input  [3:0] in_1,
  input  [3:0] in_2,
  input  [3:0] in_3,
  input  [3:0] in_4,
  output [3:0] out_5,
  output [3:0] out_6,
  output [3:0] out_7,
  output [3:0] out_8
);

  wire [3:0] n4bit_mid_1_out_3, n4bit_mid_1_out_4, n4bit_mid_2_out_3, n4bit_mid_2_out_4, n4bit_mid_3_out_3,
       n4bit_mid_4_out_3, n4bit_mid_4_out_4, n4bit_mid_5_out_3;

  _4bit_mid u_4bit_mid_1 (.in_1(in_1), .in_2(in_2), .out_3(n4bit_mid_1_out_3), .out_4(n4bit_mid_1_out_4));
  _4bit_mid u_4bit_mid_2 (.in_1(n4bit_mid_1_out_4), .in_2(in_3), .out_3(n4bit_mid_2_out_3), .out_4(n4bit_mid_2_out_4));
  _4bit_mid u_4bit_mid_3 (.in_1(n4bit_mid_2_out_4), .in_2(in_4), .out_3(n4bit_mid_3_out_3), .out_4(out_8));
  _4bit_mid u_4bit_mid_4 (
    .in_1(n4bit_mid_1_out_3), .in_2(n4bit_mid_2_out_3), .out_3(n4bit_mid_4_out_3), .out_4(n4bit_mid_4_out_4));
  _4bit_mid u_4bit_mid_5 (.in_1(n4bit_mid_4_out_4), .in_2(n4bit_mid_3_out_3), .out_3(n4bit_mid_5_out_3), .out_4(out_7));
  _4bit_mid u_4bit_mid_6 (.in_1(n4bit_mid_4_out_3), .in_2(n4bit_mid_5_out_3), .out_3(out_5), .out_4(out_6));
endmodule

module _4bit_mid (
  input  [3:0] in_1,
  input  [3:0] in_2,
  output [3:0] out_3,
  output [3:0] out_4
);

  wire comparator_1_gt;

  Comparator #(.width(4), .mode("unsigned")) comparator_1 (.a(in_1), .b(in_2), .gt(comparator_1_gt));  // open: eq, lt
  _4bit_swap u_4bit_swap_1 (.in_1(in_1), .in_2(in_2), .in_3(comparator_1_gt), .out_4(out_3), .out_5(out_4));
endmodule
