// Logisim project crc.circ as structural Verilog: 3 circuits, main circuit CRC
module CRC (
  input  [7:0] ori,
  input  [3:0] div,
  output [10:0] out_3
);

  neoDiv neodiv_1 (.ori(ori), .div(div), .out_3(out_3[2:0]));

  assign out_3[10:3] = ori;
endmodule

module neoSub (
  input  [3:0] ori,
  input  [3:0] div,
  output [2:0] result
);

  wire not_1_out;
  wire [3:0] multiplexer_1_out;

  Multiplexer #(.width(4)) multiplexer_1 (
    .in0(div), .in1(4'b0000), .out(multiplexer_1_out), .sel(not_1_out));  // open: en
  not not_1 (not_1_out, ori[3]);
  xor xor_1 (result[1], ori[1], multiplexer_1_out[1]);
  xor xor_2 (result[2], ori[2], multiplexer_1_out[2]);
  xor xor_3 (result[0], ori[0], multiplexer_1_out[0]);
endmodule

module neoDiv (
  input  [7:0] ori,
  input  [3:0] div,
  output [2:0] out_3
);

  wire [3:1] neosub_1_result, neosub_2_result, neosub_3_result, neosub_5_result, neosub_6_result,
       neosub_7_result, neosub_8_result;

  // Probe on ori[7:4]
  // Probe on {neosub_5_result, ori[3]}
  // Probe on {neosub_6_result, ori[2]}
  // Probe on {neosub_7_result, ori[1]}
  // Probe on {neosub_8_result, ori[0]}
  // Probe on {neosub_1_result, 1'b0}
  // Probe on {neosub_2_result, 1'b0}
  neoSub neosub_1 (.ori({neosub_8_result, ori[0]}), .div(div), .result(neosub_1_result));
  neoSub neosub_2 (.ori({neosub_1_result, 1'b0}), .div(div), .result(neosub_2_result));
  neoSub neosub_3 (.ori({neosub_2_result, 1'b0}), .div(div), .result(neosub_3_result));
  neoSub neosub_4 (.ori({neosub_3_result, 1'b0}), .div(div), .result(out_3));
  neoSub neosub_5 (.ori(ori[7:4]), .div(div), .result(neosub_5_result));
  neoSub neosub_6 (.ori({neosub_5_result, ori[3]}), .div(div), .result(neosub_6_result));
  neoSub neosub_7 (.ori({neosub_6_result, ori[2]}), .div(div), .result(neosub_7_result));
  neoSub neosub_8 (.ori({neosub_7_result, ori[1]}), .div(div), .result(neosub_8_result));

  // Other names for the same wires on the sheet: _4 = ori[4]; _3 = ori[5]; _2 = ori[6]; _1 = ori[7]; _8 = ori[0];
  //   _5 = ori[3]; _6 = ori[2]; _7 = ori[1]
endmodule
