// Logisim project fib.circ as structural Verilog: 1 circuit, main circuit main
module main (
  input  [2:0] in_1,
  output [3:0] out_2
);

  wire and_1_out, clock_1_out, comparator_1_eq, comparator_2_eq, counter_1_carry, counter_2_carry, not_1_out,
       not_2_out;
  wire [2:0] counter_2_q;
  wire [3:0] adder_1_out, controlled_buffer_1_out, multiplexer_1_out, multiplexer_2_out, register_1_q,
       register_2_q;

  Clock clock_1 (.out(clock_1_out));
  Multiplexer #(.width(4)) multiplexer_1 (
    .in0(register_2_q), .in1(4'b0001), .out(multiplexer_1_out), .sel(not_1_out));  // open: en
  Register #(.width(4)) register_1 (.D(multiplexer_1_out), .Q(register_1_q), .clk(clock_1_out));  // open: en, clr
  Counter #(.width(1), .max('h1), .ongoal("stay")) counter_1 (
    .carry(counter_1_carry), .clk(clock_1_out), .clr(counter_2_carry));  // open: load, D, count, Q
  Counter #(.width(3), .max('h7), .ongoal("stay")) counter_2 (
    .Q(counter_2_q), .carry(counter_2_carry), .clk(clock_1_out), .clr(not_1_out));  // open: load, D, count
  not not_1 (not_1_out, counter_1_carry);
  Comparator #(.width(3)) comparator_1 (.a(counter_2_q), .b(in_1), .eq(comparator_1_eq));  // open: gt, lt
  Adder #(.width(4)) adder_1 (.a(register_1_q), .b(register_2_q), .out(adder_1_out));  // open: cin, cout
  Register #(.width(4)) register_2 (.D(adder_1_out), .Q(register_2_q), .clk(clock_1_out), .clr(not_1_out));  // open: en
  assign controlled_buffer_1_out = comparator_1_eq ? register_2_q : 4'bz;  // Controlled_Buffer controlled_buffer_1
  not not_2 (not_2_out, counter_2_carry);
  Comparator #(.width(3)) comparator_2 (.a(in_1), .b(3'b111), .eq(comparator_2_eq));  // open: gt, lt
  Multiplexer #(.width(4)) multiplexer_2 (
    .in0(controlled_buffer_1_out), .in1(4'b1101), .out(multiplexer_2_out), .sel(and_1_out));  // open: en
  Register #(.width(4)) register_3 (.D(multiplexer_2_out), .en(not_2_out), .Q(out_2), .clk(clock_1_out));  // open: clr
  and and_1 (and_1_out, not_1_out, comparator_2_eq);
endmodule
