// Logisim project fib_challenge.circ as structural Verilog: 4 circuits, main circuit main
module main (
  input  [31:0] in_1,
  output [31:0] out_2
);

  wire clock_1_out, counter_1_q, register_1_q, signal_handler_1_current_bit, signal_handler_1_end;
  wire [31:0] get_matrix_pow_1_out_2, get_matrix_pow_1_out_3, get_matrix_pow_1_out_4, get_matrix_pow_1_out_5,
       matrix_multiplier_1_c11, matrix_multiplier_1_c12, matrix_multiplier_1_c21, matrix_multiplier_1_out_12,
       multiplexer_1_out, multiplexer_2_out, multiplexer_3_out, multiplexer_4_out, multiplexer_5_out,
       multiplexer_6_out, multiplexer_7_out, multiplexer_8_out, register_2_q, register_3_q, register_4_q,
       register_5_q;

  Clock clock_1 (.out(clock_1_out));
  Counter #(.width(1), .max('h1), .ongoal("stay")) counter_1 (
    .Q(counter_1_q), .clk(clock_1_out));  // open: load, D, count, carry, clr
  signal_handler signal_handler_1 (.in(in_1), .\end (signal_handler_1_end), .current_bit(signal_handler_1_current_bit));
  Register #(.width(1)) register_1 (.D(signal_handler_1_end), .Q(register_1_q), .clk(clock_1_out));  // open: en, clr
  get_matrix_pow get_matrix_pow_1 (
    .valid(signal_handler_1_current_bit), .out_2(get_matrix_pow_1_out_2), .out_3(get_matrix_pow_1_out_3),
    .out_4(get_matrix_pow_1_out_4), .out_5(get_matrix_pow_1_out_5));
  Multiplexer #(.width(32)) multiplexer_1 (
    .in0(get_matrix_pow_1_out_2), .in1(32'h1), .out(multiplexer_1_out), .sel(register_1_q));  // open: en
  Multiplexer #(.width(32)) multiplexer_2 (
    .in0(get_matrix_pow_1_out_3), .in1({32{1'b0}}), .out(multiplexer_2_out), .sel(register_1_q));  // open: en
  Multiplexer #(.width(32)) multiplexer_3 (
    .in0(get_matrix_pow_1_out_4), .in1({32{1'b0}}), .out(multiplexer_3_out), .sel(register_1_q));  // open: en
  Multiplexer #(.width(32)) multiplexer_4 (
    .in0(get_matrix_pow_1_out_5), .in1(32'h1), .out(multiplexer_4_out), .sel(register_1_q));  // open: en
  Multiplexer #(.width(32)) multiplexer_5 (
    .in0(32'h1), .in1(register_2_q), .out(multiplexer_5_out), .sel(counter_1_q));  // open: en
  Multiplexer #(.width(32)) multiplexer_6 (
    .in0({32{1'b0}}), .in1(register_3_q), .out(multiplexer_6_out), .sel(counter_1_q));  // open: en
  Multiplexer #(.width(32)) multiplexer_7 (
    .in0({32{1'b0}}), .in1(register_4_q), .out(multiplexer_7_out), .sel(counter_1_q));  // open: en
  Multiplexer #(.width(32)) multiplexer_8 (
    .in0(32'h1), .in1(register_5_q), .out(multiplexer_8_out), .sel(counter_1_q));  // open: en
  matrix_multiplier matrix_multiplier_1 (
    .A11(multiplexer_1_out), .A12(multiplexer_2_out), .A21(multiplexer_3_out), .A22(multiplexer_4_out),
    .B11(multiplexer_5_out), .B12(multiplexer_6_out), .B21(multiplexer_7_out), .B22(multiplexer_8_out),
    .C11(matrix_multiplier_1_c11), .C12(matrix_multiplier_1_c12), .C21(matrix_multiplier_1_c21),
    .out_12(matrix_multiplier_1_out_12));
  Register #(.width(32)) register_2 (
    .D(matrix_multiplier_1_c11), .Q(register_2_q), .clk(clock_1_out));  // open: en, clr
  Register #(.width(32)) register_3 (
    .D(matrix_multiplier_1_c12), .Q(register_3_q), .clk(clock_1_out));  // open: en, clr
  Register #(.width(32)) register_4 (
    .D(matrix_multiplier_1_c21), .Q(register_4_q), .clk(clock_1_out));  // open: en, clr
  Register #(.width(32)) register_5 (
    .D(matrix_multiplier_1_out_12), .Q(register_5_q), .clk(clock_1_out));  // open: en, clr
  Multiplexer #(.width(32)) multiplexer_9 (
    .in0({32{1'b0}}), .in1(register_4_q), .out(out_2), .sel(register_1_q));  // open: en
endmodule

module matrix_multiplier (
  input  [31:0] A11,
  input  [31:0] A12,
  input  [31:0] A21,
  input  [31:0] A22,
  input  [31:0] B11,
  input  [31:0] B12,
  input  [31:0] B21,
  input  [31:0] B22,
  output [31:0] C11,
  output [31:0] C12,
  output [31:0] C21,
  output [31:0] out_12
);

  wire [31:0] multiplier_1_out, multiplier_2_out, multiplier_3_out, multiplier_4_out, multiplier_5_out,
       multiplier_6_out, multiplier_7_out, multiplier_8_out;

  Multiplier #(.width(32)) multiplier_1 (.a(A11), .b(B11), .out(multiplier_1_out));  // open: cin, cout
  Multiplier #(.width(32)) multiplier_2 (.a(A12), .b(B21), .out(multiplier_2_out));  // open: cin, cout
  Multiplier #(.width(32)) multiplier_3 (.a(A11), .b(B12), .out(multiplier_3_out));  // open: cin, cout
  Multiplier #(.width(32)) multiplier_4 (.a(A12), .b(B22), .out(multiplier_4_out));  // open: cin, cout
  Multiplier #(.width(32)) multiplier_5 (.a(A21), .b(B11), .out(multiplier_5_out));  // open: cin, cout
  Multiplier #(.width(32)) multiplier_6 (.a(A22), .b(B21), .out(multiplier_6_out));  // open: cin, cout
  Multiplier #(.width(32)) multiplier_7 (.a(A21), .b(B12), .out(multiplier_7_out));  // open: cin, cout
  Multiplier #(.width(32)) multiplier_8 (.a(A22), .b(B22), .out(multiplier_8_out));  // open: cin, cout
  Adder #(.width(32)) adder_1 (.a(multiplier_1_out), .b(multiplier_2_out), .out(C11));  // open: cin, cout
  Adder #(.width(32)) adder_2 (.a(multiplier_3_out), .b(multiplier_4_out), .out(C12));  // open: cin, cout
  Adder #(.width(32)) adder_3 (.a(multiplier_5_out), .b(multiplier_6_out), .out(C21));  // open: cin, cout
  Adder #(.width(32)) adder_4 (.a(multiplier_7_out), .b(multiplier_8_out), .out(out_12));  // open: cin, cout
endmodule

module signal_handler (
  input  [31:0] in,
  output \end ,
  output current_bit
);

  wire clock_1_out, counter_1_q, not_1_out, not_2_out, not_3_out, shift_register_1_out;

  Clock clock_1 (.out(clock_1_out));
  Counter #(.width(1), .max('h1), .ongoal("stay")) counter_1 (
    .Q(counter_1_q), .clk(clock_1_out));  // open: load, D, count, carry, clr
  not not_1 (not_1_out, counter_1_q);
  not not_2 (not_2_out, \end );
  Shift_Register #(.length(32)) shift_register_1 (
    .shift(not_2_out), .in(shift_register_1_out), .clk(clock_1_out), .out(shift_register_1_out),
    .load(not_1_out), .d0(in[31]), .d1(in[30]), .d2(in[29]), .d3(in[28]), .d4(in[27]), .d5(in[26]),
    .d6(in[25]), .d7(in[24]), .d8(in[23]), .d9(in[22]), .d10(in[21]), .d11(in[20]), .d12(in[19]),
    .d13(in[18]), .d14(in[17]), .d15(in[16]), .d16(in[15]), .d17(in[14]), .d18(in[13]), .d19(in[12]),
    .d20(in[11]), .d21(in[10]), .d22(in[9]), .d23(in[8]), .d24(in[7]), .d25(in[6]), .d26(in[5]), .d27(in[4]),
    .d28(in[3]), .d29(in[2]), .d30(in[1]), .d31(in[0]), .q31(current_bit));  // open: clr, q0, q1, q2, q3, q4, q5, q6, q7, q8, q9, q10, q11, q12, q13, q14, q15, q16, q17, q18, q19, q20, q21, q22, q23, q24, q25, q26, q27, q28, q29, q30
  Counter #(.width(5), .max('h1f), .ongoal("stay")) counter_2 (
    .carry(\end ), .clk(clock_1_out), .clr(not_3_out));  // open: load, D, count, Q
  not not_3 (not_3_out, counter_1_q);
endmodule

module get_matrix_pow (
  input  valid,
  output [31:0] out_2,
  output [31:0] out_3,
  output [31:0] out_4,
  output [31:0] out_5
);

  wire clock_1_out, counter_1_q;
  wire [31:0] matrix_multiplier_1_c11, matrix_multiplier_1_c12, matrix_multiplier_1_c21,
       matrix_multiplier_1_out_12, multiplexer_1_out, multiplexer_2_out, multiplexer_3_out,
       multiplexer_4_out, multiplexer_5_out, multiplexer_6_out, multiplexer_7_out, multiplexer_8_out,
       register_1_q, register_2_q, register_3_q, register_4_q;

  Clock clock_1 (.out(clock_1_out));
  Counter #(.width(1), .max('h1), .ongoal("stay")) counter_1 (
    .Q(counter_1_q), .clk(clock_1_out));  // open: load, D, count, carry, clr
  Multiplexer #(.width(32)) multiplexer_1 (
    .in0(32'h1), .in1(register_1_q), .out(multiplexer_1_out), .sel(counter_1_q));  // open: en
  Multiplexer #(.width(32)) multiplexer_2 (
    .in0(32'h1), .in1(register_2_q), .out(multiplexer_2_out), .sel(counter_1_q));  // open: en
  Multiplexer #(.width(32)) multiplexer_3 (
    .in0(32'h1), .in1(register_3_q), .out(multiplexer_3_out), .sel(counter_1_q));  // open: en
  Multiplexer #(.width(32)) multiplexer_4 (
    .in0({32{1'b0}}), .in1(register_4_q), .out(multiplexer_4_out), .sel(counter_1_q));  // open: en
  Multiplexer #(.width(32)) multiplexer_5 (
    .in0(32'h1), .in1(register_1_q), .out(multiplexer_5_out), .sel(counter_1_q));  // open: en
  Multiplexer #(.width(32)) multiplexer_6 (
    .in0({32{1'b0}}), .in1(register_2_q), .out(multiplexer_6_out), .sel(counter_1_q));  // open: en
  Multiplexer #(.width(32)) multiplexer_7 (
    .in0({32{1'b0}}), .in1(register_3_q), .out(multiplexer_7_out), .sel(counter_1_q));  // open: en
  Multiplexer #(.width(32)) multiplexer_8 (
    .in0(32'h1), .in1(register_4_q), .out(multiplexer_8_out), .sel(counter_1_q));  // open: en
  matrix_multiplier matrix_multiplier_1 (
    .A11(multiplexer_5_out), .A12(multiplexer_6_out), .A21(multiplexer_7_out), .A22(multiplexer_8_out),
    .B11(multiplexer_1_out), .B12(multiplexer_2_out), .B21(multiplexer_3_out), .B22(multiplexer_4_out),
    .C11(matrix_multiplier_1_c11), .C12(matrix_multiplier_1_c12), .C21(matrix_multiplier_1_c21),
    .out_12(matrix_multiplier_1_out_12));
  Register #(.width(32)) register_1 (
    .D(matrix_multiplier_1_c11), .Q(register_1_q), .clk(clock_1_out));  // open: en, clr
  Register #(.width(32)) register_2 (
    .D(matrix_multiplier_1_c12), .Q(register_2_q), .clk(clock_1_out));  // open: en, clr
  Register #(.width(32)) register_3 (
    .D(matrix_multiplier_1_c21), .Q(register_3_q), .clk(clock_1_out));  // open: en, clr
  Register #(.width(32)) register_4 (
    .D(matrix_multiplier_1_out_12), .Q(register_4_q), .clk(clock_1_out));  // open: en, clr
  Multiplexer #(.width(32)) multiplexer_9 (.in0(32'h1), .in1(register_1_q), .out(out_2), .sel(valid));  // open: en
  Multiplexer #(.width(32)) multiplexer_10 (
    .in0({32{1'b0}}), .in1(register_2_q), .out(out_3), .sel(valid));  // open: en
  Multiplexer #(.width(32)) multiplexer_11 (
    .in0({32{1'b0}}), .in1(register_3_q), .out(out_4), .sel(valid));  // open: en
  Multiplexer #(.width(32)) multiplexer_12 (.in0(32'h1), .in1(register_4_q), .out(out_5), .sel(valid));  // open: en
endmodule
