// Logisim project fib_challenge_toy.circ as structural Verilog
module matrix_multiply (
);

  wire clock_1_out, comparator_1_gt, comparator_2_gt, counter_1_q, rom_1_data, rom_2_data;
  wire [1:0] adder_1_out, adder_2_out, bit_extender_1_out, bit_extender_2_out, bit_extender_3_out,
       counter_3_q, shifter_1_out, shifter_2_out;
  wire [2:0] counter_2_q;

  Clock clock_1 (.out(clock_1_out));
  Counter #(.width(1), .max('h1)) counter_1 (.Q(counter_1_q), .clk(clock_1_out));  // open: load, D, count, carry, clr
  assign bit_extender_1_out = {{1{1'b0}}, counter_1_q};  // Bit_Extender bit_extender_1
  Counter #(.width(3), .max('h7)) counter_2 (.Q(counter_2_q), .clk(clock_1_out));  // open: load, D, count, carry, clr
  Counter #(.width(2), .max('h3)) counter_3 (.Q(counter_3_q), .clk(clock_1_out));  // open: load, D, count, carry, clr
  assign bit_extender_2_out = {{1{1'b0}}, comparator_1_gt};  // Bit_Extender bit_extender_2
  Comparator #(.width(3), .mode("unsigned")) comparator_1 (
    .a(counter_2_q), .b(3'b011), .gt(comparator_1_gt));  // open: eq, lt
  assign bit_extender_3_out = {{1{1'b0}}, comparator_2_gt};  // Bit_Extender bit_extender_3
  Comparator #(.width(2), .mode("unsigned")) comparator_2 (
    .a(counter_3_q), .b(2'b01), .gt(comparator_2_gt));  // open: eq, lt
  Shifter #(.width(2)) shifter_1 (.in(bit_extender_2_out), .\dist (1'b1), .out(shifter_1_out));
  Shifter #(.width(2)) shifter_2 (.in(bit_extender_3_out), .\dist (1'b1), .out(shifter_2_out));
  Adder #(.width(2)) adder_1 (.a(bit_extender_1_out), .b(shifter_1_out), .out(adder_1_out));  // open: cin, cout
  Adder #(.width(2)) adder_2 (.a(shifter_2_out), .b(bit_extender_1_out), .out(adder_2_out));  // open: cin, cout
  RAM #(.addrWidth(2), .dataWidth(1), .bus("separate")) ram_1 ();  // open: addr, din, data, str, sel, clk, ld, clr
  ROM #(.addrWidth(2), .dataWidth(1)) rom_1 (.addr(adder_1_out), .data(rom_1_data));  // open: sel
  ROM #(.addrWidth(2), .dataWidth(1)) rom_2 (.addr(adder_2_out), .data(rom_2_data));  // open: sel

  // Notes on the sheet:
  //   L
  //   R
  //   contents of rom_1 (hex, n*v repeats v):
  //   1 1 1
  //   contents of rom_2 (hex, n*v repeats v):
  //   1 1 1
endmodule
