// Logisim project fsm.circ as structural Verilog: 5 circuits, main circuit fsm
module fsm (
  input  rst,
  input  [1:0] in,
  output \output 
);

  wire clock_1_out;
  wire [2:0] multiplexer_1_out, register_1_q, state_trans_1_out_3;

  Clock clock_1 (.out(clock_1_out));
  state_trans state_trans_1 (.in_1(in), .current_state(register_1_q), .out_3(state_trans_1_out_3));
  Multiplexer #(.width(3)) multiplexer_1 (
    .in0(state_trans_1_out_3), .in1(3'b000), .out(multiplexer_1_out), .sel(rst));  // open: en
  \output  output_1 (.in_1(state_trans_1_out_3), .\output (\output ));
  Register #(.width(3)) register_1 (.D(multiplexer_1_out), .Q(register_1_q), .clk(clock_1_out));  // open: en, clr
endmodule

module state_trans (
  input  [1:0] in_1,
  input  [2:0] current_state,
  output [2:0] out_3
);

  neoTrans neotrans_1 (
    .i1(in_1[1]), .i0(in_1[0]), .c2(current_state[2]), .c1(current_state[1]), .c0(current_state[0]),
    .o2(out_3[2]), .o1(out_3[1]), .o0(out_3[0]));
endmodule

module neoTrans (
  input  i1,
  input  i0,
  input  c2,
  input  c1,
  input  c0,
  output o2,
  output o1,
  output o0
);

  wire and_2_out, and_3_out, and_4_out, and_5_out, and_6_out, and_7_out, and_8_out, and_9_out, not_1_out,
       not_2_out, not_3_out, not_4_out, not_5_out, not_6_out, not_7_out, not_8_out, not_9_out, not_10_out,
       not_11_out, not_12_out, not_13_out, not_14_out, not_15_out, not_16_out, not_17_out, not_18_out,
       not_19_out, not_20_out, not_21_out;

  not not_1 (not_1_out, i0);
  not not_2 (not_2_out, c2);
  not not_3 (not_3_out, i1);
  not not_4 (not_4_out, c2);
  not not_5 (not_5_out, c1);
  not not_6 (not_6_out, i0);
  not not_7 (not_7_out, c2);
  not not_8 (not_8_out, c1);
  not not_9 (not_9_out, i0);
  not not_10 (not_10_out, c2);
  not not_11 (not_11_out, c0);
  not not_12 (not_12_out, i0);
  not not_13 (not_13_out, c2);
  not not_14 (not_14_out, c1);
  not not_15 (not_15_out, i0);
  not not_16 (not_16_out, c2);
  not not_17 (not_17_out, c0);
  not not_18 (not_18_out, i1);
  not not_19 (not_19_out, c0);
  not not_20 (not_20_out, i1);
  not not_21 (not_21_out, i1);
  and and_1 (o2, not_1_out, not_2_out, c1, c0);
  and and_2 (and_2_out, not_3_out, not_4_out, not_5_out, c0);
  and and_3 (and_3_out, not_6_out, not_7_out, not_8_out, c0);
  and and_4 (and_4_out, not_9_out, not_10_out, c1, not_11_out);
  and and_5 (and_5_out, not_12_out, not_13_out, not_14_out, c0);
  and and_6 (and_6_out, not_15_out, not_16_out, c1, not_17_out);
  and and_7 (and_7_out, not_18_out, i0, not_19_out);
  and and_8 (and_8_out, not_20_out, i0, c1);
  and and_9 (and_9_out, not_21_out, i0, c2);
  or or_1 (o1, and_2_out, and_3_out, and_4_out);
  or or_2 (o0, and_5_out, and_6_out, and_7_out, and_8_out, and_9_out);
endmodule

module \output  (
  input  [2:0] in_1,
  output \output 
);

  wire not_1_out, not_2_out;

  not not_1 (not_1_out, in_1[1]);
  not not_2 (not_2_out, in_1[0]);
  and and_1 (\output , in_1[2], not_1_out, not_2_out);
endmodule

module tb (
  input  in_1,
  input  [1:0] in_2,
  output out_3
);

  fsm fsm_1 (.rst(in_1), .in(in_2), .\output (out_3));
endmodule
