// Logisim project fti.circ as structural Verilog: 3 circuits, main circuit ftoi
module ftoi (
  input  [15:0] in_1,
  output [31:0] Output
);

  wire exp_processor_1_denormalized, exp_processor_1_infinity_nan;
  wire [4:0] exp_processor_1_output;
  wire [31:0] float_calc_1_output, multiplexer_1_out, negator_1_out;

  // Probe on in_1[9:0]
  // Probe on in_1[14:10]
  // Probe on exp_processor_1_output
  exp_processor exp_processor_1 (
    .in_1(in_1[14:10]), .Infinity_NaN(exp_processor_1_infinity_nan),
    .Denormalized(exp_processor_1_denormalized), .Output(exp_processor_1_output));
  Multiplexer #(.width(32)) multiplexer_1 (
    .in0(float_calc_1_output), .in1({32{1'b0}}), .out(multiplexer_1_out), .sel(exp_processor_1_infinity_nan));  // open: en
  float_calc float_calc_1 (
    .Denormalized(exp_processor_1_denormalized), .exp_processed(exp_processor_1_output), .In(in_1[9:0]),
    .Output(float_calc_1_output));
  Negator #(.width(32)) negator_1 (.in(multiplexer_1_out), .out(negator_1_out));
  Multiplexer #(.width(32)) multiplexer_2 (
    .in0(multiplexer_1_out), .in1(negator_1_out), .out(Output), .sel(in_1[15]));  // open: en
endmodule

module exp_processor (
  input  [4:0] in_1,
  output Infinity_NaN,
  output Denormalized,
  output [4:0] Output
);

  Subtractor #(.width(5)) subtractor_1 (.a(in_1), .b(5'b01111), .out(Output));  // open: bin, bout
  Comparator #(.width(5)) comparator_1 (.a({5{1'b1}}), .b(in_1), .eq(Infinity_NaN));  // open: gt, lt
  Comparator #(.width(5)) comparator_2 (.a(in_1), .b({5{1'b0}}), .eq(Denormalized));  // open: gt, lt
endmodule

module float_calc (
  input  Denormalized,
  input  [4:0] exp_processed,
  input  [9:0] In,
  output [31:0] Output
);

  wire comparator_1_gt;
  wire [4:0] negator_1_out;
  wire [10:10] not_1_out;
  wire [31:0] bit_extender_1_out, multiplexer_1_out, shifter_1_out, shifter_2_out;

  not not_1 (not_1_out[10], Denormalized);
  // Probe on bit_extender_1_out
  // Probe on negator_1_out
  assign bit_extender_1_out = {{21{1'b0}}, {not_1_out[10], In}};  // Bit_Extender bit_extender_1
  Negator #(.width(5)) negator_1 (.in(exp_processed), .out(negator_1_out));
  Comparator #(.width(5)) comparator_1 (.a(exp_processed), .b({5{1'b0}}), .gt(comparator_1_gt));  // open: eq, lt
  Shifter #(.width(32), .shift("lr")) shifter_1 (.in(bit_extender_1_out), .\dist (negator_1_out), .out(shifter_1_out));
  Shifter #(.width(32)) shifter_2 (.in(bit_extender_1_out), .\dist (exp_processed), .out(shifter_2_out));
  Multiplexer #(.width(32)) multiplexer_1 (
    .in0(shifter_1_out), .in1(shifter_2_out), .out(multiplexer_1_out), .sel(comparator_1_gt));  // open: en
  Shifter #(.width(32), .shift("lr")) shifter_3 (.in(multiplexer_1_out), .\dist (5'b01010), .out(Output));
endmodule
