// Logisim project grf.circ as structural Verilog: 2 circuits, main circuit tb
module tb (
  input  en,
  input  rs,
  input  [4:0] out1,
  input  [4:0] out2,
  input  [4:0] in,
  input  [31:0] in_6,
  output [31:0] out_7,
  output [31:0] out_8
);

  wire clock_1_out;

  Clock clock_1 (.out(clock_1_out));
  grf grf_1 (
    .A1(out1), .A2(out2), .A3(in), .wb(in_6), .clk(clock_1_out), .reset(rs), .en(en), .rd1(out_7), .RD2(out_8));
endmodule

module grf (
  input  clk,
  input  reset,
  input  en,
  input  [4:0] A1,
  input  [4:0] A2,
  input  [4:0] A3,
  input  [31:0] wb,
  output [31:0] rd1,
  output [31:0] RD2
);

  wire comparator_1_eq, comparator_2_eq, comparator_3_eq, comparator_4_eq, comparator_5_eq, comparator_6_eq,
       comparator_7_eq, comparator_8_eq, comparator_9_eq, comparator_10_eq, comparator_11_eq,
       comparator_12_eq, comparator_13_eq, comparator_14_eq, comparator_15_eq, comparator_16_eq,
       comparator_17_eq, comparator_18_eq, comparator_19_eq, comparator_20_eq, comparator_21_eq,
       comparator_22_eq, comparator_23_eq, comparator_24_eq, comparator_25_eq, comparator_26_eq,
       comparator_27_eq, comparator_28_eq, comparator_29_eq, comparator_30_eq, comparator_31_eq,
       comparator_32_eq;
  wire [31:0] i0, i1, i2, i3, i4, i5, i6, i7, i8, i9, i10, i11, i12, i13, i14, i15, i16, i17, i18, i19, i20,
       i21, i22, i23, i24, i25, i26, i27, i28, i29, i30, i31, multiplexer_3_out, multiplexer_4_out,
       multiplexer_5_out, multiplexer_6_out, multiplexer_7_out, multiplexer_8_out, multiplexer_9_out,
       multiplexer_10_out, multiplexer_11_out, multiplexer_12_out, multiplexer_13_out, multiplexer_14_out,
       multiplexer_15_out, multiplexer_16_out, multiplexer_17_out, multiplexer_18_out, multiplexer_19_out,
       multiplexer_20_out, multiplexer_21_out, multiplexer_22_out, multiplexer_23_out, multiplexer_24_out,
       multiplexer_25_out, multiplexer_26_out, multiplexer_27_out, multiplexer_28_out, multiplexer_29_out,
       multiplexer_30_out, multiplexer_31_out, multiplexer_32_out, multiplexer_33_out, multiplexer_34_out,
       o0, o1, o2, o3, o4, o5, o6, o7, o8, o9, o10, o11, o12, o13, o14, o15, o16, o17, o18, o19, o20, o21,
       o22, o23, o24, o25, o26, o27, o28, o29, o30, o31;

  Demultiplexer #(.select(5), .width(32)) demultiplexer_1 (
    .out0(i0), .out1(i1), .out2(i2), .out3(i3), .out4(i4), .out5(i5), .out6(i6), .out7(i7), .out8(i8),
    .out9(i9), .out10(i10), .out11(i11), .out12(i12), .out13(i13), .out14(i14), .out15(i15), .out16(i16),
    .out17(i17), .out18(i18), .out19(i19), .out20(i20), .out21(i21), .out22(i22), .out23(i23), .out24(i24),
    .out25(i25), .out26(i26), .out27(i27), .out28(i28), .out29(i29), .out30(i30), .out31(i31), .in(wb),
    .sel(A3));  // open: en
  Multiplexer #(.select(5), .width(32)) multiplexer_1 (
    .in0(o0), .in1(o1), .in2(o2), .in3(o3), .in4(o4), .in5(o5), .in6(o6), .in7(o7), .in8(o8), .in9(o9),
    .in10(o10), .in11(o11), .in12(o12), .in13(o13), .in14(o14), .in15(o15), .in16(o16), .in17(o17),
    .in18(o18), .in19(o19), .in20(o20), .in21(o21), .in22(o22), .in23(o23), .in24(o24), .in25(o25),
    .in26(o26), .in27(o27), .in28(o28), .in29(o29), .in30(o30), .in31(o31), .out(rd1), .sel(A1));  // open: en
  Multiplexer #(.select(5), .width(32)) multiplexer_2 (
    .in0(o0), .in1(o1), .in2(o2), .in3(o3), .in4(o4), .in5(o5), .in6(o6), .in7(o7), .in8(o8), .in9(o9),
    .in10(o10), .in11(o11), .in12(o12), .in13(o13), .in14(o14), .in15(o15), .in16(o16), .in17(o17),
    .in18(o18), .in19(o19), .in20(o20), .in21(o21), .in22(o22), .in23(o23), .in24(o24), .in25(o25),
    .in26(o26), .in27(o27), .in28(o28), .in29(o29), .in30(o30), .in31(o31), .out(RD2), .sel(A2));  // open: en
  Multiplexer #(.width(32)) multiplexer_3 (
    .in0(o0), .in1(i0), .out(multiplexer_3_out), .sel(comparator_1_eq));  // open: en
  Multiplexer #(.width(32)) multiplexer_4 (
    .in0(o4), .in1(i4), .out(multiplexer_4_out), .sel(comparator_2_eq));  // open: en
  Multiplexer #(.width(32)) multiplexer_5 (
    .in0(o8), .in1(i8), .out(multiplexer_5_out), .sel(comparator_3_eq));  // open: en
  Multiplexer #(.width(32)) multiplexer_6 (
    .in0(o12), .in1(i12), .out(multiplexer_6_out), .sel(comparator_4_eq));  // open: en
  Multiplexer #(.width(32)) multiplexer_7 (
    .in0(o16), .in1(i16), .out(multiplexer_7_out), .sel(comparator_5_eq));  // open: en
  Multiplexer #(.width(32)) multiplexer_8 (
    .in0(o20), .in1(i20), .out(multiplexer_8_out), .sel(comparator_6_eq));  // open: en
  Multiplexer #(.width(32)) multiplexer_9 (
    .in0(o24), .in1(i24), .out(multiplexer_9_out), .sel(comparator_7_eq));  // open: en
  Multiplexer #(.width(32)) multiplexer_10 (
    .in0(o28), .in1(i28), .out(multiplexer_10_out), .sel(comparator_8_eq));  // open: en
  Register #(.width(32)) register_1 (.D(multiplexer_3_out), .en(en), .Q(o0), .clk(clk), .clr(1'b1));
  Comparator #(.width(5), .mode("unsigned")) comparator_1 (
    .a(A3), .b({5{1'b0}}), .eq(comparator_1_eq));  // open: gt, lt
  Register #(.width(32)) register_2 (.D(multiplexer_4_out), .en(en), .Q(o4), .clk(clk), .clr(reset));
  Comparator #(.width(5), .mode("unsigned")) comparator_2 (.a(A3), .b(5'b00100), .eq(comparator_2_eq));  // open: gt, lt
  Register #(.width(32)) register_3 (.D(multiplexer_5_out), .en(en), .Q(o8), .clk(clk), .clr(reset));
  Comparator #(.width(5), .mode("unsigned")) comparator_3 (.a(A3), .b(5'b01000), .eq(comparator_3_eq));  // open: gt, lt
  Register #(.width(32)) register_4 (.D(multiplexer_6_out), .en(en), .Q(o12), .clk(clk), .clr(reset));
  Comparator #(.width(5), .mode("unsigned")) comparator_4 (.a(A3), .b(5'b01100), .eq(comparator_4_eq));  // open: gt, lt
  Register #(.width(32)) register_5 (.D(multiplexer_7_out), .en(en), .Q(o16), .clk(clk), .clr(reset));
  Comparator #(.width(5), .mode("unsigned")) comparator_5 (.a(A3), .b(5'b10000), .eq(comparator_5_eq));  // open: gt, lt
  Register #(.width(32)) register_6 (.D(multiplexer_8_out), .en(en), .Q(o20), .clk(clk), .clr(reset));
  Comparator #(.width(5), .mode("unsigned")) comparator_6 (.a(A3), .b(5'b10100), .eq(comparator_6_eq));  // open: gt, lt
  Register #(.width(32)) register_7 (.D(multiplexer_9_out), .en(en), .Q(o24), .clk(clk), .clr(reset));
  Comparator #(.width(5), .mode("unsigned")) comparator_7 (.a(A3), .b(5'b11000), .eq(comparator_7_eq));  // open: gt, lt
  Register #(.width(32)) register_8 (.D(multiplexer_10_out), .en(en), .Q(o28), .clk(clk), .clr(reset));
  Comparator #(.width(5), .mode("unsigned")) comparator_8 (.a(A3), .b(5'b11100), .eq(comparator_8_eq));  // open: gt, lt
  Multiplexer #(.width(32)) multiplexer_11 (
    .in0(o1), .in1(i1), .out(multiplexer_11_out), .sel(comparator_9_eq));  // open: en
  Register #(.width(32)) register_9 (.D(multiplexer_11_out), .en(en), .Q(o1), .clk(clk), .clr(reset));
  Comparator #(.width(5), .mode("unsigned")) comparator_9 (.a(A3), .b(5'b00001), .eq(comparator_9_eq));  // open: gt, lt
  Multiplexer #(.width(32)) multiplexer_12 (
    .in0(o5), .in1(i5), .out(multiplexer_12_out), .sel(comparator_10_eq));  // open: en
  Register #(.width(32)) register_10 (.D(multiplexer_12_out), .en(en), .Q(o5), .clk(clk), .clr(reset));
  Multiplexer #(.width(32)) multiplexer_13 (
    .in0(o9), .in1(i9), .out(multiplexer_13_out), .sel(comparator_11_eq));  // open: en
  Register #(.width(32)) register_11 (.D(multiplexer_13_out), .en(en), .Q(o9), .clk(clk), .clr(reset));
  Multiplexer #(.width(32)) multiplexer_14 (
    .in0(o13), .in1(i13), .out(multiplexer_14_out), .sel(comparator_12_eq));  // open: en
  Register #(.width(32)) register_12 (.D(multiplexer_14_out), .en(en), .Q(o13), .clk(clk), .clr(reset));
  Multiplexer #(.width(32)) multiplexer_15 (
    .in0(o17), .in1(i17), .out(multiplexer_15_out), .sel(comparator_13_eq));  // open: en
  Register #(.width(32)) register_13 (.D(multiplexer_15_out), .en(en), .Q(o17), .clk(clk), .clr(reset));
  Multiplexer #(.width(32)) multiplexer_16 (
    .in0(o21), .in1(i21), .out(multiplexer_16_out), .sel(comparator_14_eq));  // open: en
  Multiplexer #(.width(32)) multiplexer_17 (
    .in0(o25), .in1(i25), .out(multiplexer_17_out), .sel(comparator_15_eq));  // open: en
  Multiplexer #(.width(32)) multiplexer_18 (
    .in0(o29), .in1(i29), .out(multiplexer_18_out), .sel(comparator_16_eq));  // open: en
  Comparator #(.width(5), .mode("unsigned")) comparator_10 (
    .a(A3), .b(5'b00101), .eq(comparator_10_eq));  // open: gt, lt
  Comparator #(.width(5), .mode("unsigned")) comparator_11 (
    .a(A3), .b(5'b01001), .eq(comparator_11_eq));  // open: gt, lt
  Comparator #(.width(5), .mode("unsigned")) comparator_12 (
    .a(A3), .b(5'b01101), .eq(comparator_12_eq));  // open: gt, lt
  Comparator #(.width(5), .mode("unsigned")) comparator_13 (
    .a(A3), .b(5'b10001), .eq(comparator_13_eq));  // open: gt, lt
  Register #(.width(32)) register_14 (.D(multiplexer_16_out), .en(en), .Q(o21), .clk(clk), .clr(reset));
  Comparator #(.width(5), .mode("unsigned")) comparator_14 (
    .a(A3), .b(5'b10101), .eq(comparator_14_eq));  // open: gt, lt
  Register #(.width(32)) register_15 (.D(multiplexer_17_out), .en(en), .Q(o25), .clk(clk), .clr(reset));
  Comparator #(.width(5), .mode("unsigned")) comparator_15 (
    .a(A3), .b(5'b11001), .eq(comparator_15_eq));  // open: gt, lt
  Register #(.width(32)) register_16 (.D(multiplexer_18_out), .en(en), .Q(o29), .clk(clk), .clr(reset));
  Comparator #(.width(5), .mode("unsigned")) comparator_16 (
    .a(A3), .b(5'b11101), .eq(comparator_16_eq));  // open: gt, lt
  Multiplexer #(.width(32)) multiplexer_19 (
    .in0(o2), .in1(i2), .out(multiplexer_19_out), .sel(comparator_17_eq));  // open: en
  Register #(.width(32)) register_17 (.D(multiplexer_19_out), .en(en), .Q(o2), .clk(clk), .clr(reset));
  Multiplexer #(.width(32)) multiplexer_20 (
    .in0(o6), .in1(i6), .out(multiplexer_20_out), .sel(comparator_18_eq));  // open: en
  Multiplexer #(.width(32)) multiplexer_21 (
    .in0(o10), .in1(i10), .out(multiplexer_21_out), .sel(comparator_19_eq));  // open: en
  Multiplexer #(.width(32)) multiplexer_22 (
    .in0(o14), .in1(i14), .out(multiplexer_22_out), .sel(comparator_20_eq));  // open: en
  Multiplexer #(.width(32)) multiplexer_23 (
    .in0(o18), .in1(i18), .out(multiplexer_23_out), .sel(comparator_21_eq));  // open: en
  Multiplexer #(.width(32)) multiplexer_24 (
    .in0(o22), .in1(i22), .out(multiplexer_24_out), .sel(comparator_22_eq));  // open: en
  Multiplexer #(.width(32)) multiplexer_25 (
    .in0(o26), .in1(i26), .out(multiplexer_25_out), .sel(comparator_23_eq));  // open: en
  Multiplexer #(.width(32)) multiplexer_26 (
    .in0(o30), .in1(i30), .out(multiplexer_26_out), .sel(comparator_24_eq));  // open: en
  Comparator #(.width(5), .mode("unsigned")) comparator_17 (
    .a(A3), .b(5'b00010), .eq(comparator_17_eq));  // open: gt, lt
  Register #(.width(32)) register_18 (.D(multiplexer_20_out), .en(en), .Q(o6), .clk(clk), .clr(reset));
  Comparator #(.width(5), .mode("unsigned")) comparator_18 (
    .a(A3), .b(5'b00110), .eq(comparator_18_eq));  // open: gt, lt
  Register #(.width(32)) register_19 (.D(multiplexer_21_out), .en(en), .Q(o10), .clk(clk), .clr(reset));
  Comparator #(.width(5), .mode("unsigned")) comparator_19 (
    .a(A3), .b(5'b01010), .eq(comparator_19_eq));  // open: gt, lt
  Register #(.width(32)) register_20 (.D(multiplexer_22_out), .en(en), .Q(o14), .clk(clk), .clr(reset));
  Comparator #(.width(5), .mode("unsigned")) comparator_20 (
    .a(A3), .b(5'b01110), .eq(comparator_20_eq));  // open: gt, lt
  Register #(.width(32)) register_21 (.D(multiplexer_23_out), .en(en), .Q(o18), .clk(clk), .clr(reset));
  Comparator #(.width(5), .mode("unsigned")) comparator_21 (
    .a(A3), .b(5'b10010), .eq(comparator_21_eq));  // open: gt, lt
  Register #(.width(32)) register_22 (.D(multiplexer_24_out), .en(en), .Q(o22), .clk(clk), .clr(reset));
  Comparator #(.width(5), .mode("unsigned")) comparator_22 (
    .a(A3), .b(5'b10110), .eq(comparator_22_eq));  // open: gt, lt
  Register #(.width(32)) register_23 (.D(multiplexer_25_out), .en(en), .Q(o26), .clk(clk), .clr(reset));
  Comparator #(.width(5), .mode("unsigned")) comparator_23 (
    .a(A3), .b(5'b11010), .eq(comparator_23_eq));  // open: gt, lt
  Register #(.width(32)) register_24 (.D(multiplexer_26_out), .en(en), .Q(o30), .clk(clk), .clr(reset));
  Comparator #(.width(5), .mode("unsigned")) comparator_24 (
    .a(A3), .b(5'b11110), .eq(comparator_24_eq));  // open: gt, lt
  Multiplexer #(.width(32)) multiplexer_27 (
    .in0(o3), .in1(i3), .out(multiplexer_27_out), .sel(comparator_25_eq));  // open: en
  Multiplexer #(.width(32)) multiplexer_28 (
    .in0(o7), .in1(i7), .out(multiplexer_28_out), .sel(comparator_26_eq));  // open: en
  Multiplexer #(.width(32)) multiplexer_29 (
    .in0(o11), .in1(i11), .out(multiplexer_29_out), .sel(comparator_27_eq));  // open: en
  Multiplexer #(.width(32)) multiplexer_30 (
    .in0(o15), .in1(i15), .out(multiplexer_30_out), .sel(comparator_28_eq));  // open: en
  Multiplexer #(.width(32)) multiplexer_31 (
    .in0(o19), .in1(i19), .out(multiplexer_31_out), .sel(comparator_29_eq));  // open: en
  Multiplexer #(.width(32)) multiplexer_32 (
    .in0(o23), .in1(i23), .out(multiplexer_32_out), .sel(comparator_30_eq));  // open: en
  Multiplexer #(.width(32)) multiplexer_33 (
    .in0(o27), .in1(i27), .out(multiplexer_33_out), .sel(comparator_31_eq));  // open: en
  Multiplexer #(.width(32)) multiplexer_34 (
    .in0(o31), .in1(i31), .out(multiplexer_34_out), .sel(comparator_32_eq));  // open: en
  Register #(.width(32)) register_25 (.D(multiplexer_27_out), .en(en), .Q(o3), .clk(clk), .clr(reset));
  Comparator #(.width(5), .mode("unsigned")) comparator_25 (
    .a(A3), .b(5'b00011), .eq(comparator_25_eq));  // open: gt, lt
  Register #(.width(32)) register_26 (.D(multiplexer_28_out), .en(en), .Q(o7), .clk(clk), .clr(reset));
  Comparator #(.width(5), .mode("unsigned")) comparator_26 (
    .a(A3), .b(5'b00111), .eq(comparator_26_eq));  // open: gt, lt
  Register #(.width(32)) register_27 (.D(multiplexer_29_out), .en(en), .Q(o11), .clk(clk), .clr(reset));
  Comparator #(.width(5), .mode("unsigned")) comparator_27 (
    .a(A3), .b(5'b01011), .eq(comparator_27_eq));  // open: gt, lt
  Register #(.width(32)) register_28 (.D(multiplexer_30_out), .en(en), .Q(o15), .clk(clk), .clr(reset));
  Comparator #(.width(5), .mode("unsigned")) comparator_28 (
    .a(A3), .b(5'b01111), .eq(comparator_28_eq));  // open: gt, lt
  Register #(.width(32)) register_29 (.D(multiplexer_31_out), .en(en), .Q(o19), .clk(clk), .clr(reset));
  Comparator #(.width(5), .mode("unsigned")) comparator_29 (
    .a(A3), .b(5'b10011), .eq(comparator_29_eq));  // open: gt, lt
  Register #(.width(32)) register_30 (.D(multiplexer_32_out), .en(en), .Q(o23), .clk(clk), .clr(reset));
  Comparator #(.width(5), .mode("unsigned")) comparator_30 (
    .a(A3), .b(5'b10111), .eq(comparator_30_eq));  // open: gt, lt
  Register #(.width(32)) register_31 (.D(multiplexer_33_out), .en(en), .Q(o27), .clk(clk), .clr(reset));
  Comparator #(.width(5), .mode("unsigned")) comparator_31 (
    .a(A3), .b(5'b11011), .eq(comparator_31_eq));  // open: gt, lt
  Register #(.width(32)) register_32 (.D(multiplexer_34_out), .en(en), .Q(o31), .clk(clk), .clr(reset));
  Comparator #(.width(5), .mode("unsigned")) comparator_32 (
    .a(A3), .b({5{1'b1}}), .eq(comparator_32_eq));  // open: gt, lt

  // Other names for the same wires on the sheet: in[4:0] = A3
endmodule
