// Logisim project mod5.circ as structural Verilog: 3 circuits, main circuit mod5_bak
module decode (
  input  in_1,
  input  in_2,
  output S1,
  output S2,
  output S3,
  output S4
);

  wire xor_1_out;

  xor xor_1 (xor_1_out, in_1, in_2);
  nor nor_1 (S1, in_1, in_2);
  and and_1 (S3, in_1, in_2);
  and and_2 (S2, in_2, xor_1_out);
  and and_3 (S4, in_1, xor_1_out);
endmodule

module mod5_bak (
  input  In,
  output s0,
  output s1,
  output s2,
  output s3,
  output s4
);

  wire shift_register_1_q0, shift_register_1_q1;

  Shift_Register #(.length(2)) shift_register_1 (
    .in(In), .q0(shift_register_1_q0), .q1(shift_register_1_q1));  // open: shift, clk, out, load, clr, d0, d1
  decode decode (.in_1(shift_register_1_q1), .in_2(shift_register_1_q0), .S1(s1), .S2(s2), .S3(s3), .S4(s4));

  assign s0 = 1'b0;
endmodule

module mod5 (
  input  In,
  output s0,
  output s1,
  output s2,
  output s3,
  output s4
);

  wire clock_1_out, register_1_q;

  Clock clock_1 (.out(clock_1_out));
  Register #(.width(1)) register_1 (.D(In), .Q(register_1_q), .clk(clock_1_out));  // open: en, clr
  decode decode (.in_1(register_1_q), .in_2(In), .S1(s1), .S2(s2), .S3(s3), .S4(s4));

  assign s0 = 1'b0;
endmodule
