// Logisim project navi.circ as structural Verilog: 3 circuits, main circuit navigation
module navigation (
  input  [1:0] in_1,
  input  clk,
  input  reset,
  output arrive,
  output hit
);

  wire multiplexer_7_out, multiplexer_8_out, multiplexer_9_out, multiplexer_10_out, multiplexer_11_out,
       multiplexer_12_out, multiplexer_13_out, multiplexer_14_out, multiplexer_15_out, multiplexer_16_out,
       multiplexer_17_out, multiplexer_18_out;
  wire [2:0] multiplexer_1_out, multiplexer_2_out, multiplexer_3_out, multiplexer_4_out, multiplexer_5_out,
       multiplexer_6_out, register_1_q;

  Multiplexer #(.select(2), .width(3)) multiplexer_1 (
    .in0(3'b010), .in1(3'b000), .in2(3'b000), .in3(3'b000), .out(multiplexer_1_out), .sel(in_1));  // open: en
  Multiplexer #(.select(2), .width(3)) multiplexer_2 (
    .in0(3'b000), .in1(3'b000), .in2(3'b000), .in3(3'b000), .out(multiplexer_2_out), .sel(in_1));  // open: en
  Multiplexer #(.select(2), .width(3)) multiplexer_3 (
    .in0(3'b100), .in1(3'b011), .in2(3'b000), .in3(3'b010), .out(multiplexer_3_out), .sel(in_1));  // open: en
  Multiplexer #(.select(2), .width(3)) multiplexer_4 (
    .in0(3'b001), .in1(3'b011), .in2(3'b011), .in3(3'b010), .out(multiplexer_4_out), .sel(in_1));  // open: en
  Multiplexer #(.select(2), .width(3)) multiplexer_5 (
    .in0(3'b100), .in1(3'b001), .in2(3'b010), .in3(3'b100), .out(multiplexer_5_out), .sel(in_1));  // open: en
  Register #(.width(3)) register_1 (.D(multiplexer_6_out), .Q(register_1_q), .clk(clk), .clr(reset));  // open: en
  Multiplexer #(.select(3), .width(3)) multiplexer_6 (
    .in0(multiplexer_1_out), .in1(multiplexer_2_out), .in2(multiplexer_3_out), .in3(multiplexer_4_out),
    .in4(multiplexer_5_out), .in5(3'b000), .in6(3'b000), .in7(3'b000), .out(multiplexer_6_out),
    .sel(register_1_q));  // open: en
  Multiplexer #(.select(2)) multiplexer_7 (
    .in0(1'b0), .in1(1'b0), .in2(1'b0), .in3(1'b0), .out(multiplexer_7_out), .sel(in_1));  // open: en
  Multiplexer #(.select(2)) multiplexer_8 (
    .in0(1'b0), .in1(1'b0), .in2(1'b0), .in3(1'b0), .out(multiplexer_8_out), .sel(in_1));  // open: en
  Multiplexer #(.select(2)) multiplexer_9 (
    .in0(1'b0), .in1(1'b0), .in2(1'b0), .in3(1'b0), .out(multiplexer_9_out), .sel(in_1));  // open: en
  Multiplexer #(.select(2)) multiplexer_10 (
    .in0(1'b1), .in1(1'b0), .in2(1'b0), .in3(1'b0), .out(multiplexer_10_out), .sel(in_1));  // open: en
  Multiplexer #(.select(2)) multiplexer_11 (
    .in0(1'b0), .in1(1'b1), .in2(1'b0), .in3(1'b0), .out(multiplexer_11_out), .sel(in_1));  // open: en
  Multiplexer #(.select(2)) multiplexer_12 (
    .in0(1'b0), .in1(1'b1), .in2(1'b1), .in3(1'b1), .out(multiplexer_12_out), .sel(in_1));  // open: en
  Multiplexer #(.select(2)) multiplexer_13 (
    .in0(1'b0), .in1(1'b0), .in2(1'b0), .in3(1'b0), .out(multiplexer_13_out), .sel(in_1));  // open: en
  Multiplexer #(.select(2)) multiplexer_14 (
    .in0(1'b0), .in1(1'b0), .in2(1'b0), .in3(1'b1), .out(multiplexer_14_out), .sel(in_1));  // open: en
  Multiplexer #(.select(2)) multiplexer_15 (
    .in0(1'b0), .in1(1'b1), .in2(1'b1), .in3(1'b0), .out(multiplexer_15_out), .sel(in_1));  // open: en
  Multiplexer #(.select(2)) multiplexer_16 (
    .in0(1'b1), .in1(1'b0), .in2(1'b0), .in3(1'b1), .out(multiplexer_16_out), .sel(in_1));  // open: en
  Multiplexer #(.select(3)) multiplexer_17 (
    .in0(multiplexer_7_out), .in1(multiplexer_8_out), .in2(multiplexer_9_out), .in3(multiplexer_10_out),
    .in4(multiplexer_11_out), .out(multiplexer_17_out), .sel(register_1_q));  // open: in5, in6, in7, en
  Multiplexer #(.select(3)) multiplexer_18 (
    .in0(multiplexer_12_out), .in1(multiplexer_13_out), .in2(multiplexer_14_out), .in3(multiplexer_15_out),
    .in4(multiplexer_16_out), .out(multiplexer_18_out), .sel(register_1_q));  // open: in5, in6, in7, en
  Register #(.width(1)) register_2 (.D(multiplexer_17_out), .Q(arrive), .clk(clk), .clr(reset));  // open: en
  Register #(.width(1)) register_3 (.D(multiplexer_18_out), .Q(hit), .clk(clk), .clr(reset));  // open: en
endmodule

module experiment (
);

  wire [1:0] undriven;
  wire [2:0] adder_1_out, multiplexer_2_out, multiplexer_3_out, subtractor_1_out, undriven_2;

  Multiplexer multiplexer_1 (.sel(undriven[1]));  // open: in0, in1, out, en
  Multiplexer #(.select(2), .width(3)) multiplexer_2 (
    .in0(3'b010), .in1(3'b001), .in2(3'b010), .in3(3'b001), .out(multiplexer_2_out), .sel(undriven));  // open: en
  Adder #(.width(3)) adder_1 (.a(multiplexer_2_out), .b(undriven_2), .out(adder_1_out));  // open: cin, cout
  Subtractor #(.width(3)) subtractor_1 (
    .a(multiplexer_2_out), .b(undriven_2), .out(subtractor_1_out));  // open: bin, bout
  Multiplexer #(.width(3)) multiplexer_3 (
    .in0(adder_1_out), .in1(subtractor_1_out), .out(multiplexer_3_out), .sel(undriven[0]));  // open: en
endmodule

module tb (
  input  [1:0] in_1,
  input  rst,
  output arri,
  output hit
);

  wire clock_1_out;

  Clock clock_1 (.out(clock_1_out));
  navigation navigation_1 (.in_1(in_1), .clk(clock_1_out), .reset(rst), .arrive(arri), .hit(hit));
endmodule
