// Logisim project single_loop_bak.circ as structural Verilog: 16 circuits, main circuit main
module main (
  input  rst,
  output [31:0] Instr,
  output [31:0] pc,
  output RegWrite,
  output [4:0] RegAddr,
  output [31:0] RegData,
  output MemWrite,
  output [31:0] MemAddr,
  output [31:0] MemData
);

  wire clk, CMP_EQ, CMP_LT, is_sign, MALUB_c, MGRFA3_c, MGRFWD_c;
  wire [3:0] alu_c_t, alu_sa_c, npc_c;
  wire [4:0] MALUSA, rd, rs, rt, sa, undriven_3;
  wire [15:0] imm16;
  wire [25:0] undriven_2;
  wire [31:0] DM_O, EXT_B, GRF_A1, MALUB, NPC, PC_4, undriven;

  Clock clock_1 (.out(clk));
  NPC npc_1 (
    .PC(pc), .IMM16(imm16), .IMM26(undriven_2), .JA(undriven), .EQ(CMP_EQ), .LT(CMP_LT), .NPCOp(npc_c),
    .NPC(NPC), .PC_4(PC_4));
  IFU ifu_1 (.NPC(NPC), .clk(clk), .rst(rst), .INS(Instr), .PC(pc));
  Multiplexer #(.width(5)) multiplexer_1 (.in0(rt), .in1(rd), .out(RegAddr), .sel(MGRFA3_c));  // open: en
  Multiplexer #(.width(32)) multiplexer_2 (.in0(MemAddr), .in1(DM_O), .out(RegData), .sel(MGRFWD_c));  // open: en
  GRF GRF (
    .A1(rs), .A2(rt), .A3(RegAddr), .WD(RegData), .clk(clk), .rst(rst), .we(RegWrite), .RD1(GRF_A1),
    .RD2(MemData));
  EXT EXT (.A(imm16), .EXTOp(is_sign), .B(EXT_B));
  CTRL ctrl_1 (
    .INS(Instr), .rs(rs), .rt(rt), .rd(rd), .sa(sa), .imm16(imm16), .npc_c(npc_c), .alu_c(alu_c_t),
    .alu_sa_c(alu_sa_c), .MGRFA3_c(MGRFA3_c), .is_ltr(RegWrite), .MGRFWD_c(MGRFWD_c), .is_sign(is_sign),
    .is_stm(MemWrite), .MALUB_c(MALUB_c));  // open: opcode, funct, imm26, is_stm_2, is_stm_3
  ALU ALU (.A(GRF_A1), .B(MALUB), .SHAMT(MALUSA), .ALUOp(alu_c_t), .C(MemAddr));
  CMP cmp_1 (.A1(GRF_A1), .A2(MemData), .EQ(CMP_EQ), .LT(CMP_LT));
  Multiplexer #(.width(32)) multiplexer_3 (.in0(EXT_B), .in1(MemData), .out(MALUB), .sel(MALUB_c));  // open: en
  Multiplexer #(.select(4), .width(5)) multiplexer_4 (
    .in0(sa), .in1(5'b10000), .in2(undriven_3), .out(MALUSA), .sel(alu_sa_c));  // open: in3, in4, in5, in6, in7, in8, in9, in10, in11, in12, in13, in14, in15, en
  DM DM (.ADDR(MemAddr), .WD(MemData), .WE(MemWrite), .clk(clk), .rst(rst), .O(DM_O));

  // Other names for the same wires on the sheet: ALU_C[31:0] = MemAddr; GRF_A2[31:0] = MemData; is_ltr = RegWrite;
  //   is_stm = MemWrite; MGRFA3[4:0] = RegAddr; MGRFWD[31:0] = RegData

  // Notes on the sheet:
  //   MGRF
  //   MALU
endmodule

module ALU (
  input  [31:0] A,
  input  [31:0] B,
  input  [4:0] SHAMT,
  input  [3:0] ALUOp,
  output [31:0] C
);

  wire [31:0] adder_1_out, or_1_out, shifter_1_out, subtractor_1_out;

  Adder #(.width(32)) adder_1 (.a(A), .b(B), .out(adder_1_out));  // open: cin, cout
  Subtractor #(.width(32)) subtractor_1 (.a(A), .b(B), .out(subtractor_1_out));  // open: bin, bout
  assign or_1_out = A | B;  // OR_Gate or_1, 32 bits wide
  Shifter #(.width(32)) shifter_1 (.in(B), .\dist (SHAMT), .out(shifter_1_out));
  Multiplexer #(.select(4), .width(32)) multiplexer_1 (
    .in0(adder_1_out), .in1(subtractor_1_out), .in2(or_1_out), .in3(shifter_1_out), .out(C), .sel(ALUOp));  // open: in4, in5, in6, in7, in8, in9, in10, in11, in12, in13, in14, in15, en

  // Notes on the sheet:
  //   RS
  //   RT/IMM
endmodule

module EXT (
  input  [15:0] A,
  input  EXTOp,
  output [31:0] B
);

  wire [31:0] bit_extender_1_out, bit_extender_2_out;

  assign bit_extender_1_out = {{16{1'b0}}, A};  // Bit_Extender bit_extender_1
  assign bit_extender_2_out = {{16{A[15]}}, A};  // Bit_Extender bit_extender_2
  Multiplexer #(.width(32)) multiplexer_1 (
    .in0(bit_extender_1_out), .in1(bit_extender_2_out), .out(B), .sel(EXTOp));  // open: en
endmodule

module GRF (
  input  [4:0] A1,
  input  [4:0] A2,
  input  [4:0] A3,
  input  [31:0] WD,
  input  clk,
  input  rst,
  input  we,
  output [31:0] RD1,
  output [31:0] RD2
);

  wire comparator_1_eq, comparator_2_eq, comparator_3_eq, comparator_4_eq, comparator_5_eq, comparator_6_eq,
       comparator_7_eq, comparator_8_eq, comparator_9_eq, comparator_10_eq, comparator_11_eq,
       comparator_12_eq, comparator_13_eq, comparator_14_eq, comparator_15_eq, comparator_16_eq,
       comparator_17_eq, comparator_18_eq, comparator_19_eq, comparator_20_eq, comparator_21_eq,
       comparator_22_eq, comparator_23_eq, comparator_24_eq, comparator_25_eq, comparator_26_eq,
       comparator_27_eq, comparator_28_eq, comparator_29_eq, comparator_30_eq, comparator_31_eq,
       comparator_32_eq;
  wire [31:0] i0, i1, i2, i3, i4, i5, i6, i7, i8, i9, i10, i11, i12, i13, i14, i15, i16, i17, i18, i19, i20,
       i21, i22, i23, i24, i25, i26, i27, i28, i29, i30, i31, multiplexer_3_out, multiplexer_4_out,
       multiplexer_5_out, multiplexer_6_out, multiplexer_7_out, multiplexer_8_out, multiplexer_9_out,
       multiplexer_10_out, multiplexer_11_out, multiplexer_12_out, multiplexer_13_out, multiplexer_14_out,
       multiplexer_15_out, multiplexer_16_out, multiplexer_17_out, multiplexer_18_out, multiplexer_19_out,
       multiplexer_20_out, multiplexer_21_out, multiplexer_22_out, multiplexer_23_out, multiplexer_24_out,
       multiplexer_25_out, multiplexer_26_out, multiplexer_27_out, multiplexer_28_out, multiplexer_29_out,
       multiplexer_30_out, multiplexer_31_out, multiplexer_32_out, multiplexer_33_out, multiplexer_34_out,
       o0, o1, o2, o3, o4, o5, o6, o7, o8, o9, o10, o11, o12, o13, o14, o15, o16, o17, o18, o19, o20, o21,
       o22, o23, o24, o25, o26, o27, o28, o29, o30, o31;

  Demultiplexer #(.select(5), .width(32)) demultiplexer_1 (
    .out0(i0), .out1(i1), .out2(i2), .out3(i3), .out4(i4), .out5(i5), .out6(i6), .out7(i7), .out8(i8),
    .out9(i9), .out10(i10), .out11(i11), .out12(i12), .out13(i13), .out14(i14), .out15(i15), .out16(i16),
    .out17(i17), .out18(i18), .out19(i19), .out20(i20), .out21(i21), .out22(i22), .out23(i23), .out24(i24),
    .out25(i25), .out26(i26), .out27(i27), .out28(i28), .out29(i29), .out30(i30), .out31(i31), .in(WD),
    .sel(A3));  // open: en
  Multiplexer #(.select(5), .width(32)) multiplexer_1 (
    .in0(o0), .in1(o1), .in2(o2), .in3(o3), .in4(o4), .in5(o5), .in6(o6), .in7(o7), .in8(o8), .in9(o9),
    .in10(o10), .in11(o11), .in12(o12), .in13(o13), .in14(o14), .in15(o15), .in16(o16), .in17(o17),
    .in18(o18), .in19(o19), .in20(o20), .in21(o21), .in22(o22), .in23(o23), .in24(o24), .in25(o25),
    .in26(o26), .in27(o27), .in28(o28), .in29(o29), .in30(o30), .in31(o31), .out(RD1), .sel(A1));  // open: en
  Multiplexer #(.select(5), .width(32)) multiplexer_2 (
    .in0(o0), .in1(o1), .in2(o2), .in3(o3), .in4(o4), .in5(o5), .in6(o6), .in7(o7), .in8(o8), .in9(o9),
    .in10(o10), .in11(o11), .in12(o12), .in13(o13), .in14(o14), .in15(o15), .in16(o16), .in17(o17),
    .in18(o18), .in19(o19), .in20(o20), .in21(o21), .in22(o22), .in23(o23), .in24(o24), .in25(o25),
    .in26(o26), .in27(o27), .in28(o28), .in29(o29), .in30(o30), .in31(o31), .out(RD2), .sel(A2));  // open: en
  Multiplexer #(.width(32)) multiplexer_3 (
    .in0(o0), .in1(i0), .out(multiplexer_3_out), .sel(comparator_1_eq));  // open: en
  Multiplexer #(.width(32)) multiplexer_4 (
    .in0(o4), .in1(i4), .out(multiplexer_4_out), .sel(comparator_2_eq));  // open: en
  Multiplexer #(.width(32)) multiplexer_5 (
    .in0(o8), .in1(i8), .out(multiplexer_5_out), .sel(comparator_3_eq));  // open: en
  Multiplexer #(.width(32)) multiplexer_6 (
    .in0(o12), .in1(i12), .out(multiplexer_6_out), .sel(comparator_4_eq));  // open: en
  Multiplexer #(.width(32)) multiplexer_7 (
    .in0(o16), .in1(i16), .out(multiplexer_7_out), .sel(comparator_5_eq));  // open: en
  Multiplexer #(.width(32)) multiplexer_8 (
    .in0(o20), .in1(i20), .out(multiplexer_8_out), .sel(comparator_6_eq));  // open: en
  Multiplexer #(.width(32)) multiplexer_9 (
    .in0(o24), .in1(i24), .out(multiplexer_9_out), .sel(comparator_7_eq));  // open: en
  Multiplexer #(.width(32)) multiplexer_10 (
    .in0(o28), .in1(i28), .out(multiplexer_10_out), .sel(comparator_8_eq));  // open: en
  Register #(.width(32)) register_1 (.D(multiplexer_3_out), .en(we), .Q(o0), .clk(clk), .clr(1'b1));
  Comparator #(.width(5), .mode("unsigned")) comparator_1 (
    .a(A3), .b({5{1'b0}}), .eq(comparator_1_eq));  // open: gt, lt
  Register #(.width(32)) register_2 (.D(multiplexer_4_out), .en(we), .Q(o4), .clk(clk), .clr(rst));
  Comparator #(.width(5), .mode("unsigned")) comparator_2 (.a(A3), .b(5'b00100), .eq(comparator_2_eq));  // open: gt, lt
  Register #(.width(32)) register_3 (.D(multiplexer_5_out), .en(we), .Q(o8), .clk(clk), .clr(rst));
  Comparator #(.width(5), .mode("unsigned")) comparator_3 (.a(A3), .b(5'b01000), .eq(comparator_3_eq));  // open: gt, lt
  Register #(.width(32)) register_4 (.D(multiplexer_6_out), .en(we), .Q(o12), .clk(clk), .clr(rst));
  Comparator #(.width(5), .mode("unsigned")) comparator_4 (.a(A3), .b(5'b01100), .eq(comparator_4_eq));  // open: gt, lt
  Register #(.width(32)) register_5 (.D(multiplexer_7_out), .en(we), .Q(o16), .clk(clk), .clr(rst));
  Comparator #(.width(5), .mode("unsigned")) comparator_5 (.a(A3), .b(5'b10000), .eq(comparator_5_eq));  // open: gt, lt
  Register #(.width(32)) register_6 (.D(multiplexer_8_out), .en(we), .Q(o20), .clk(clk), .clr(rst));
  Comparator #(.width(5), .mode("unsigned")) comparator_6 (.a(A3), .b(5'b10100), .eq(comparator_6_eq));  // open: gt, lt
  Register #(.width(32)) register_7 (.D(multiplexer_9_out), .en(we), .Q(o24), .clk(clk), .clr(rst));
  Comparator #(.width(5), .mode("unsigned")) comparator_7 (.a(A3), .b(5'b11000), .eq(comparator_7_eq));  // open: gt, lt
  Register #(.width(32)) register_8 (.D(multiplexer_10_out), .en(we), .Q(o28), .clk(clk), .clr(rst));
  Comparator #(.width(5), .mode("unsigned")) comparator_8 (.a(A3), .b(5'b11100), .eq(comparator_8_eq));  // open: gt, lt
  Multiplexer #(.width(32)) multiplexer_11 (
    .in0(o1), .in1(i1), .out(multiplexer_11_out), .sel(comparator_9_eq));  // open: en
  Register #(.width(32)) register_9 (.D(multiplexer_11_out), .en(we), .Q(o1), .clk(clk), .clr(rst));
  Comparator #(.width(5), .mode("unsigned")) comparator_9 (.a(A3), .b(5'b00001), .eq(comparator_9_eq));  // open: gt, lt
  Multiplexer #(.width(32)) multiplexer_12 (
    .in0(o5), .in1(i5), .out(multiplexer_12_out), .sel(comparator_10_eq));  // open: en
  Register #(.width(32)) register_10 (.D(multiplexer_12_out), .en(we), .Q(o5), .clk(clk), .clr(rst));
  Multiplexer #(.width(32)) multiplexer_13 (
    .in0(o9), .in1(i9), .out(multiplexer_13_out), .sel(comparator_11_eq));  // open: en
  Register #(.width(32)) register_11 (.D(multiplexer_13_out), .en(we), .Q(o9), .clk(clk), .clr(rst));
  Multiplexer #(.width(32)) multiplexer_14 (
    .in0(o13), .in1(i13), .out(multiplexer_14_out), .sel(comparator_12_eq));  // open: en
  Register #(.width(32)) register_12 (.D(multiplexer_14_out), .en(we), .Q(o13), .clk(clk), .clr(rst));
  Multiplexer #(.width(32)) multiplexer_15 (
    .in0(o17), .in1(i17), .out(multiplexer_15_out), .sel(comparator_13_eq));  // open: en
  Register #(.width(32)) register_13 (.D(multiplexer_15_out), .en(we), .Q(o17), .clk(clk), .clr(rst));
  Multiplexer #(.width(32)) multiplexer_16 (
    .in0(o21), .in1(i21), .out(multiplexer_16_out), .sel(comparator_14_eq));  // open: en
  Multiplexer #(.width(32)) multiplexer_17 (
    .in0(o25), .in1(i25), .out(multiplexer_17_out), .sel(comparator_15_eq));  // open: en
  Multiplexer #(.width(32)) multiplexer_18 (
    .in0(o29), .in1(i29), .out(multiplexer_18_out), .sel(comparator_16_eq));  // open: en
  Comparator #(.width(5), .mode("unsigned")) comparator_10 (
    .a(A3), .b(5'b00101), .eq(comparator_10_eq));  // open: gt, lt
  Comparator #(.width(5), .mode("unsigned")) comparator_11 (
    .a(A3), .b(5'b01001), .eq(comparator_11_eq));  // open: gt, lt
  Comparator #(.width(5), .mode("unsigned")) comparator_12 (
    .a(A3), .b(5'b01101), .eq(comparator_12_eq));  // open: gt, lt
  Comparator #(.width(5), .mode("unsigned")) comparator_13 (
    .a(A3), .b(5'b10001), .eq(comparator_13_eq));  // open: gt, lt
  Register #(.width(32)) register_14 (.D(multiplexer_16_out), .en(we), .Q(o21), .clk(clk), .clr(rst));
  Comparator #(.width(5), .mode("unsigned")) comparator_14 (
    .a(A3), .b(5'b10101), .eq(comparator_14_eq));  // open: gt, lt
  Register #(.width(32)) register_15 (.D(multiplexer_17_out), .en(we), .Q(o25), .clk(clk), .clr(rst));
  Comparator #(.width(5), .mode("unsigned")) comparator_15 (
    .a(A3), .b(5'b11001), .eq(comparator_15_eq));  // open: gt, lt
  Register #(.width(32)) register_16 (.D(multiplexer_18_out), .en(we), .Q(o29), .clk(clk), .clr(rst));
  Comparator #(.width(5), .mode("unsigned")) comparator_16 (
    .a(A3), .b(5'b11101), .eq(comparator_16_eq));  // open: gt, lt
  Multiplexer #(.width(32)) multiplexer_19 (
    .in0(o2), .in1(i2), .out(multiplexer_19_out), .sel(comparator_17_eq));  // open: en
  Register #(.width(32)) register_17 (.D(multiplexer_19_out), .en(we), .Q(o2), .clk(clk), .clr(rst));
  Multiplexer #(.width(32)) multiplexer_20 (
    .in0(o6), .in1(i6), .out(multiplexer_20_out), .sel(comparator_18_eq));  // open: en
  Multiplexer #(.width(32)) multiplexer_21 (
    .in0(o10), .in1(i10), .out(multiplexer_21_out), .sel(comparator_19_eq));  // open: en
  Multiplexer #(.width(32)) multiplexer_22 (
    .in0(o14), .in1(i14), .out(multiplexer_22_out), .sel(comparator_20_eq));  // open: en
  Multiplexer #(.width(32)) multiplexer_23 (
    .in0(o18), .in1(i18), .out(multiplexer_23_out), .sel(comparator_21_eq));  // open: en
  Multiplexer #(.width(32)) multiplexer_24 (
    .in0(o22), .in1(i22), .out(multiplexer_24_out), .sel(comparator_22_eq));  // open: en
  Multiplexer #(.width(32)) multiplexer_25 (
    .in0(o26), .in1(i26), .out(multiplexer_25_out), .sel(comparator_23_eq));  // open: en
  Multiplexer #(.width(32)) multiplexer_26 (
    .in0(o30), .in1(i30), .out(multiplexer_26_out), .sel(comparator_24_eq));  // open: en
  Comparator #(.width(5), .mode("unsigned")) comparator_17 (
    .a(A3), .b(5'b00010), .eq(comparator_17_eq));  // open: gt, lt
  Register #(.width(32)) register_18 (.D(multiplexer_20_out), .en(we), .Q(o6), .clk(clk), .clr(rst));
  Comparator #(.width(5), .mode("unsigned")) comparator_18 (
    .a(A3), .b(5'b00110), .eq(comparator_18_eq));  // open: gt, lt
  Register #(.width(32)) register_19 (.D(multiplexer_21_out), .en(we), .Q(o10), .clk(clk), .clr(rst));
  Comparator #(.width(5), .mode("unsigned")) comparator_19 (
    .a(A3), .b(5'b01010), .eq(comparator_19_eq));  // open: gt, lt
  Register #(.width(32)) register_20 (.D(multiplexer_22_out), .en(we), .Q(o14), .clk(clk), .clr(rst));
  Comparator #(.width(5), .mode("unsigned")) comparator_20 (
    .a(A3), .b(5'b01110), .eq(comparator_20_eq));  // open: gt, lt
  Register #(.width(32)) register_21 (.D(multiplexer_23_out), .en(we), .Q(o18), .clk(clk), .clr(rst));
  Comparator #(.width(5), .mode("unsigned")) comparator_21 (
    .a(A3), .b(5'b10010), .eq(comparator_21_eq));  // open: gt, lt
  Register #(.width(32)) register_22 (.D(multiplexer_24_out), .en(we), .Q(o22), .clk(clk), .clr(rst));
  Comparator #(.width(5), .mode("unsigned")) comparator_22 (
    .a(A3), .b(5'b10110), .eq(comparator_22_eq));  // open: gt, lt
  Register #(.width(32)) register_23 (.D(multiplexer_25_out), .en(we), .Q(o26), .clk(clk), .clr(rst));
  Comparator #(.width(5), .mode("unsigned")) comparator_23 (
    .a(A3), .b(5'b11010), .eq(comparator_23_eq));  // open: gt, lt
  Register #(.width(32)) register_24 (.D(multiplexer_26_out), .en(we), .Q(o30), .clk(clk), .clr(rst));
  Comparator #(.width(5), .mode("unsigned")) comparator_24 (
    .a(A3), .b(5'b11110), .eq(comparator_24_eq));  // open: gt, lt
  Multiplexer #(.width(32)) multiplexer_27 (
    .in0(o3), .in1(i3), .out(multiplexer_27_out), .sel(comparator_25_eq));  // open: en
  Multiplexer #(.width(32)) multiplexer_28 (
    .in0(o7), .in1(i7), .out(multiplexer_28_out), .sel(comparator_26_eq));  // open: en
  Multiplexer #(.width(32)) multiplexer_29 (
    .in0(o11), .in1(i11), .out(multiplexer_29_out), .sel(comparator_27_eq));  // open: en
  Multiplexer #(.width(32)) multiplexer_30 (
    .in0(o15), .in1(i15), .out(multiplexer_30_out), .sel(comparator_28_eq));  // open: en
  Multiplexer #(.width(32)) multiplexer_31 (
    .in0(o19), .in1(i19), .out(multiplexer_31_out), .sel(comparator_29_eq));  // open: en
  Multiplexer #(.width(32)) multiplexer_32 (
    .in0(o23), .in1(i23), .out(multiplexer_32_out), .sel(comparator_30_eq));  // open: en
  Multiplexer #(.width(32)) multiplexer_33 (
    .in0(o27), .in1(i27), .out(multiplexer_33_out), .sel(comparator_31_eq));  // open: en
  Multiplexer #(.width(32)) multiplexer_34 (
    .in0(o31), .in1(i31), .out(multiplexer_34_out), .sel(comparator_32_eq));  // open: en
  Register #(.width(32)) register_25 (.D(multiplexer_27_out), .en(we), .Q(o3), .clk(clk), .clr(rst));
  Comparator #(.width(5), .mode("unsigned")) comparator_25 (
    .a(A3), .b(5'b00011), .eq(comparator_25_eq));  // open: gt, lt
  Register #(.width(32)) register_26 (.D(multiplexer_28_out), .en(we), .Q(o7), .clk(clk), .clr(rst));
  Comparator #(.width(5), .mode("unsigned")) comparator_26 (
    .a(A3), .b(5'b00111), .eq(comparator_26_eq));  // open: gt, lt
  Register #(.width(32)) register_27 (.D(multiplexer_29_out), .en(we), .Q(o11), .clk(clk), .clr(rst));
  Comparator #(.width(5), .mode("unsigned")) comparator_27 (
    .a(A3), .b(5'b01011), .eq(comparator_27_eq));  // open: gt, lt
  Register #(.width(32)) register_28 (.D(multiplexer_30_out), .en(we), .Q(o15), .clk(clk), .clr(rst));
  Comparator #(.width(5), .mode("unsigned")) comparator_28 (
    .a(A3), .b(5'b01111), .eq(comparator_28_eq));  // open: gt, lt
  Register #(.width(32)) register_29 (.D(multiplexer_31_out), .en(we), .Q(o19), .clk(clk), .clr(rst));
  Comparator #(.width(5), .mode("unsigned")) comparator_29 (
    .a(A3), .b(5'b10011), .eq(comparator_29_eq));  // open: gt, lt
  Register #(.width(32)) register_30 (.D(multiplexer_32_out), .en(we), .Q(o23), .clk(clk), .clr(rst));
  Comparator #(.width(5), .mode("unsigned")) comparator_30 (
    .a(A3), .b(5'b10111), .eq(comparator_30_eq));  // open: gt, lt
  Register #(.width(32)) register_31 (.D(multiplexer_33_out), .en(we), .Q(o27), .clk(clk), .clr(rst));
  Comparator #(.width(5), .mode("unsigned")) comparator_31 (
    .a(A3), .b(5'b11011), .eq(comparator_31_eq));  // open: gt, lt
  Register #(.width(32)) register_32 (.D(multiplexer_34_out), .en(we), .Q(o31), .clk(clk), .clr(rst));
  Comparator #(.width(5), .mode("unsigned")) comparator_32 (
    .a(A3), .b({5{1'b1}}), .eq(comparator_32_eq));  // open: gt, lt

  // Other names for the same wires on the sheet: in[4:0] = A3
endmodule

module IFU (
  input  [31:0] NPC,
  input  clk,
  input  rst,
  output [31:0] INS,
  output [31:0] PC
);

  wire [13:2] PC_q;
  wire [31:0] subtractor_1_out;

  Subtractor #(.width(32)) subtractor_1 (.a(NPC), .b(32'h3000), .out(subtractor_1_out));  // open: bin, bout
  Register #(.width(12)) u_PC (.D(subtractor_1_out[13:2]), .Q(PC_q), .clk(clk), .clr(rst));  // open: en
  ROM #(.addrWidth(12), .dataWidth(32)) rom_1 (.addr(PC_q), .data(INS));  // open: sel
  Adder #(.width(32)) adder_1 (.a({{18{1'b0}}, PC_q, 2'b00}), .b(32'h3000), .out(PC));  // open: cin, cout

  // Notes on the sheet:
  //   contents of rom_1 (hex, n*v repeats v):
  //   3c190ea6 f56022 3c0aa289 8c190600 356bd7cc 1171fffd 0 16aa820 274d020 3c177397 1973022 8c0c0f44
  //   35ca2de1 356b5a76 1176fff4 0 ac0c10ac ac0721cc 3c06dc24 1d38020 3487c86d 8c0e0d70 10f4820 28c4022
  //   4*0 372d820 e5d822 6e8020 17aa822 132d822 3721020 cb7820 12a4822 36b43bfe 352994cb 112effdd ac180d6c
  //   ac041c8c 8c031148 8c1b0a20 3c033cda 36b54a3f 12b9ffd5 34c6d00e 10d7ffd4 3c0aedc8 3c0caa72 3c06be7e 0
  //   0 ac09061c 3c094372 0 8c100c60 0 2ac8020 8c0a199c ac1a1cb0 2431822 34a5e0a9 10b5ffd3 3c0c12ad
  //   8c142d08 8c1726e0 3718d22d 130dfffd 35292a76 1128ffd0 8c0a2ecc 0 299b022 3c1a54cb 0 2493822 372b9abc
  //   8c09020c 129c022 3c10f35e 1305020 8c101548 36b54e0f 12b3ffed ac1211a8 ac100abc 0 ac1024b4 3c17074f
  //   26e6022 8c112fa0 8c142280 3c14a342 689822 2701822 36d6ee4d 12d2ffe0 ac131e94 36104bd9 121affb9
  //   3c16f27f ac090d7c 0 348c020 3c0bd1ac 8c0227ac 3694d8bf 128fff97 3c0c5597 2eaa822 ac0b2320 14cb020
  //   36940462 1286ffa4 3c08699e 35ce50d1 11caffc7 0 3c167980 0 b6b820 2282020 c37822 18f2020 3c10671a
  //   28b7820 3508e59c 1115ff96 345518e5 37244796 114c022 0 8c16020c 3c0bea70 0 d12020 ac0812cc ac0d0c74 0
  //   ac16164c 3c0ada5b 3c188477 0 ac0721d4 2b77822 0 34a53ffa 10baffd8 0 0 0 36516857 2da9820 1628822
  //   3164822 3c16c3a6 0 1cd2022 377b56b0 1378ff62 3c1b47a5 0 377ba117 1371ffb4 35291119 112effc3 3c03b8d0
  //   3647ce9e 35efda0e 11e5fffc 36adb2b2 3484a04d 108dff70 32bb020 368f77f9 ac1206b4 ac1806b8 3c199cc0
  //   1276020 0 8c122474 36f7ba85 12f0ff8a 36c647f0 8c131784 ac1a2e0c ac082170 0 35f774cf 188a822 377b62f0
  //   1368ffb9 ac090078 8c032990 248c820 8c192f0c ac18109c f42820 3463a32a 106dff74 34add4ef 3c02de26
  //   8c182e38 3664020 354a5f8e 1150ff8c 303a022 ac151bd0 3c093e3b 8c112344 ac04279c 8c1a169c 1868820
  //   172d022 8c1218bc 3c0cda07 14f2820 8c0d0784 364f2875 356b2951 117bffc9 36d61887 12d2fff8 8c0e14e4
  //   365c822 1029020 358358b4 0 305a822 19ba020 2c4d822 ac0d2b4c 34d5c287 367338ed 1269ffcf 26c1822
  //   1e73820 0 20e6820 3c0b8bf9 8c0d1168 375aac14 134effdb ac0312ec 2f62022 2dbc822 8c021468 8c132ca8 0
  //   2549020 8c0a2ce0 ac17109c 2181020 4e2022 0 ac101590 3c0d2c53 3c14221f 1c86820 ac0f09d8 344e4d82
  //   ac0a19e0 34f36142 34cc4927 8c09032c 3610f14d 1203ff4f 8c180b00 358ceafe 1185ff6b ac0e272c ac06007c
  //   34b977df 0 8c1b26e4 0 18c4020 358cb8c0 1194feeb ac0427c8 361085cc 1214fefc 8c121938 0 34842f5b
  //   1085ff7e ac1302a0 1539022 2b49022 ac131374 34e73ffe 8c181204 36d69a46 ac0c06f4 356bb76c 8c082a70 0
  //   177d022 358f24ef 3c032401 377b6907 1365ff2c 376372c4 0 364fe1f4 1724822 8c1909ac 3743b165 3c0be49e 0
  //   3c1b2b6a 8c071e70 1449820 26a7820 3c159bae 3738cff3 8c0b2844 2c8b822 8c181df0 0 346c020 36730c30
  //   126fffdc 3c1b3e06 ac03275c 8c191cdc 0 377b1ee4 1369ff8e 2cc9022 3285022 ac16241c 3442b939 1052ff1a
  //   1519822 14db020 74d020 ac0718b4 0 718822 ac0c1cdc 1c68022 d35822 352c8fa1 3c0dfb6a ac1512b8 3729e2e3
  //   35adf0c4 11a4ffd6 3c0ca376 3c1179cd ac0b20a0 12c5822 8c160b68 34aaa700 ac1a0b20 8c1a2b2c 8c101cbc
  //   ac0a2cc0 8c0308d8 3c11e554 ac1229c4 3c18d7db 8c062894 0 34c27f56 2b07820 0 3166820 ac0f0de8 36ea0e66
  //   3673fda3 1271ff04 363153c1 1225ffac 36f735bf 12f5fff8 34e701bd 3694921c 1290fe87 0 8c042e78 10f6822
  //   36d6dec8 12cdffbb 34a5b5f4 10bbffee 36d619e0 12c6fee4 35ade694 11b9ffa7 375a67c4 1353ff5c 0 ac160c94
  //   8c0e0254 3c12535c 3c085483 ac062ebc ac181c70 3c0731de 0 0 35294e23 1138ff50 2517022 e24022 f8d820
  //   ac1a21d4 8c071630 34843914 1092ff7f ac162178 3c0d1e83 361010b6 1204fec9 ac1602c4 ac1a2ed0 8c0d1bac
  //   ac181158 35ad0bf2 11b5ff3f 0 36edf917 ecc022 35ac648d 799822 8c0c2a00 34e7dd1a 10e3fef8 3c18cccf
  //   304d022 27a8820 2d61022 0 1115820 3c103ce1 8c1a0ec8 8c1222ec 3c053544 0 3032020 0 ac1a11bc 1ef6020
  //   ac0d14f4 ac1a2420 8c0b04ec ac1a1d70 36ab93b4 35075543 34425046 1046ff4a 8c032338 3442181e 1050fffb
  //   18fd822 0 8c132b6c 358c4e3a 1186ff0a 2759020 22bd022 36e7e603 8c082ef8 374d7a1f 3c036f16 ac082708
  //   3c12f044 3c064404 8c0e2c0c 3c0b4003 1da9820 ac18296c ac072718 34e7e787 10ecfefa 8c1a217c 0 ac0d0970
  //   0 35b9f3eb 36ed09ab 0 0 37571c1f 1069020 1739020 3c075a5c ac1627c8 8c0e0ef4 ac052b74
endmodule

module NPC (
  input  [31:0] PC,
  input  [15:0] IMM16,
  input  [25:0] IMM26,
  input  [31:0] JA,
  input  EQ,
  input  LT,
  input  [3:0] NPCOp,
  output [31:0] NPC,
  output [31:0] PC_4
);

  wire [31:0] adder_2_out, bit_extender_1_out, multiplexer_1_out;

  // Probe on {IMM16, 2'b00}
  assign bit_extender_1_out = {{14{IMM16[15]}}, {IMM16, 2'b00}};  // Bit_Extender bit_extender_1
  Adder #(.width(32)) adder_1 (.a(PC), .b(32'h4), .out(PC_4));  // open: cin, cout
  Adder #(.width(32)) adder_2 (.a(PC_4), .b(bit_extender_1_out), .out(adder_2_out));  // open: cin, cout
  Multiplexer #(.width(32)) multiplexer_1 (
    .in0(PC_4), .in1(adder_2_out), .out(multiplexer_1_out), .sel(EQ));  // open: en
  Multiplexer #(.select(4), .width(32)) multiplexer_2 (
    .in0(PC_4), .in1(multiplexer_1_out), .out(NPC), .sel(NPCOp));  // open: in2, in3, in4, in5, in6, in7, in8, in9, in10, in11, in12, in13, in14, in15, en
endmodule

module CMP (
  input  [31:0] A1,
  input  [31:0] A2,
  output EQ,
  output LT
);

  Comparator #(.width(32)) comparator_1 (.a(A1), .b(A2), .eq(EQ), .lt(LT));  // open: gt
endmodule

module DM (
  input  [31:0] ADDR,
  input  clk,
  input  rst,
  input  WE,
  input  [31:0] WD,
  output [31:0] O
);

  RAM #(.addrWidth(12), .dataWidth(32), .bus("separate")) ram_1 (
    .addr(ADDR[13:2]), .din(WD), .data(O), .str(WE), .clk(clk), .clr(rst));  // open: sel, ld
endmodule

module CTRL_DEC (
  input  [31:0] INS,
  output [5:0] opcode,
  output [4:0] rs,
  output [4:0] rt,
  output [4:0] rd,
  output [4:0] sa,
  output [5:0] funct,
  output [15:0] imm16,
  output [25:0] imm26
);


  assign funct = INS[5:0];
  assign imm16 = INS[15:0];
  assign imm26 = INS[25:0];
  assign opcode = INS[31:26];
  assign rd = INS[15:11];
  assign rs = INS[25:21];
  assign rt = INS[20:16];
  assign sa = INS[10:6];
endmodule

module CTRL_AND (
  input  [5:0] opcode,
  input  [5:0] funct,
  output r_ins,
  output add,
  output sub,
  output sll,
  output beq,
  output lui,
  output lw,
  output sw,
  output ori,
  output bezal,
  output slo,
  output lwor
);

  wire comparator_2_eq, comparator_3_eq, comparator_4_eq;

  Comparator #(.width(6)) comparator_1 (.a(opcode), .b({6{1'b0}}), .eq(r_ins));  // open: gt, lt
  Comparator #(.width(6)) comparator_2 (.a(funct), .b(6'b100000), .eq(comparator_2_eq));  // open: gt, lt
  Comparator #(.width(6)) comparator_3 (.a(funct), .b(6'b100010), .eq(comparator_3_eq));  // open: gt, lt
  Comparator #(.width(6)) comparator_4 (.a(funct), .b({6{1'b0}}), .eq(comparator_4_eq));  // open: gt, lt
  Comparator #(.width(6)) comparator_5 (.a(funct), .b(6'b110001), .eq(bezal));  // open: gt, lt
  Comparator #(.width(6)) comparator_6 (.a(funct), .b(6'b101010), .eq(slo));  // open: gt, lt
  and and_1 (add, r_ins, comparator_2_eq);
  and and_2 (sub, r_ins, comparator_3_eq);
  and and_3 (sll, r_ins, comparator_4_eq);
  Comparator #(.width(6)) comparator_7 (.a(opcode), .b(6'b000100), .eq(beq));  // open: gt, lt
  Comparator #(.width(6)) comparator_8 (.a(opcode), .b(6'b001111), .eq(lui));  // open: gt, lt
  Comparator #(.width(6)) comparator_9 (.a(opcode), .b(6'b100011), .eq(lw));  // open: gt, lt
  Comparator #(.width(6)) comparator_10 (.a(opcode), .b(6'b101011), .eq(sw));  // open: gt, lt
  Comparator #(.width(6)) comparator_11 (.a(opcode), .b(6'b001101), .eq(ori));  // open: gt, lt
  Comparator #(.width(6)) comparator_12 (.a(opcode), .b(6'b101101), .eq(lwor));  // open: gt, lt
endmodule

module CTRL_OR (
  input  r_ins,
  input  add,
  input  sub,
  input  sll,
  input  beq,
  input  lui,
  input  lw,
  input  sw,
  input  ori,
  input  bezal,
  input  slo,
  input  lwor,
  output [3:0] npc_c,
  output [3:0] alu_c,
  output [3:0] alu_sa_c,
  output is_r_ins,
  output is_ltr,
  output is_lfm,
  output is_sign,
  output is_stm
);

  wire not_ltr_out, or_1_out, or_2_out, or_3_out, or_4_out, or_5_out, or_6_out, or_7_out, or_8_out, or_9_out,
       or_10_out;

  or or_1 (or_1_out, add, bezal, slo);
  buf or_2 (or_2_out, sub);  // OR_Gate
  buf or_3 (or_3_out, lwor);  // OR_Gate
  or or_4 (or_4_out, sll, lui);
  buf or_5 (or_5_out, beq);  // OR_Gate
  // OR_Gate or_6 has open pins: out=or_6_out
  // OR_Gate or_7 has open pins: out=or_7_out
  buf or_8 (or_8_out, sll);  // OR_Gate
  buf or_9 (or_9_out, lui);  // OR_Gate
  // OR_Gate or_10 has open pins: out=or_10_out
  npc_c npc_c_1 (.b(or_5_out), .j(1'b0), .i(1'b0), .npc_c(npc_c));
  alu_sa_c alu_sa_c_1 (.shamt(or_8_out), .dec16(or_9_out), .v(1'b0), .alu_sa_c(alu_sa_c));
  alu_c alu_c_1 (.alu_add(or_1_out), .alu_sub(or_2_out), .alu_ori(or_3_out), .alu_sll(or_4_out), .alu_c(alu_c));
  or not_ltr (not_ltr_out, slo, beq);
  buf or_11 (is_lfm, bezal);  // OR_Gate
  or or_12 (is_sign, bezal, slo);
  buf or_13 (is_stm, slo);  // OR_Gate
  not not_1 (is_ltr, not_ltr_out);

  assign is_r_ins = r_ins;
  assign lw = bezal;
  assign ori = lwor;
  assign sw = slo;

  // Other names for the same wires on the sheet: rins = r_ins
endmodule

module CTRL (
  input  [31:0] INS,
  output [5:0] opcode,
  output [4:0] rs,
  output [4:0] rt,
  output [4:0] rd,
  output [4:0] sa,
  output [5:0] funct,
  output [15:0] imm16,
  output [25:0] imm26,
  output [3:0] npc_c,
  output [3:0] alu_c,
  output [3:0] alu_sa_c,
  output MGRFA3_c,
  output is_ltr,
  output MGRFWD_c,
  output is_sign,
  output is_stm,
  output MALUB_c,
  output is_stm_2,
  output is_stm_3
);

  wire ctrl_and_1_add, ctrl_and_1_beq, ctrl_and_1_bezal, ctrl_and_1_lui, ctrl_and_1_lw, ctrl_and_1_ori,
       ctrl_and_1_r_ins, ctrl_and_1_sll, ctrl_and_1_sub, ctrl_and_1_sw, undriven;

  CTRL_DEC ctrl_dec_1 (
    .INS(INS), .opcode(opcode), .rs(rs), .rt(rt), .rd(rd), .sa(sa), .funct(funct), .imm16(imm16),
    .imm26(imm26));
  CTRL_AND ctrl_and_1 (
    .opcode(opcode), .funct(funct), .r_ins(ctrl_and_1_r_ins), .add(ctrl_and_1_add), .sub(ctrl_and_1_sub),
    .sll(ctrl_and_1_sll), .beq(ctrl_and_1_beq), .lui(ctrl_and_1_lui), .lw(ctrl_and_1_lw), .sw(ctrl_and_1_sw),
    .ori(ctrl_and_1_ori), .bezal(ctrl_and_1_bezal));  // open: slo, lwor
  CTRL_OR ctrl_or_1 (
    .r_ins(ctrl_and_1_r_ins), .add(ctrl_and_1_add), .sub(ctrl_and_1_sub), .sll(ctrl_and_1_sll),
    .beq(ctrl_and_1_beq), .lui(ctrl_and_1_lui), .lw(ctrl_and_1_lw), .sw(ctrl_and_1_sw), .ori(ctrl_and_1_ori),
    .npc_c(npc_c), .alu_c(alu_c), .alu_sa_c(alu_sa_c), .is_r_ins(MALUB_c), .is_ltr(is_ltr),
    .is_lfm(MGRFWD_c), .is_sign(is_sign), .is_stm(is_stm), .bezal(ctrl_and_1_bezal));  // open: slo, lwor
  mgrfa3cc mgrfa3cc_1 (.r_ins(MALUB_c), .bezal(undriven));  // open: o1, o0
endmodule

module alu_c (
  input  alu_add,
  input  alu_sub,
  input  alu_ori,
  input  alu_sll,
  output [3:0] alu_c
);

  wire not_1_out, not_2_out, not_3_out, not_4_out;

  not not_1 (not_1_out, alu_add);
  and and_1 (alu_c[1], not_1_out, not_2_out);
  not not_2 (not_2_out, alu_sub);
  not not_3 (not_3_out, alu_add);
  and and_2 (alu_c[0], not_3_out, not_4_out);
  not not_4 (not_4_out, alu_ori);

  assign alu_c[3:2] = 2'b00;
endmodule

module npc_c (
  input  b,
  input  j,
  input  i,
  output [3:0] npc_c
);

  or or_1 (npc_c[1], i, j);
  or or_2 (npc_c[0], i, b);

  assign npc_c[3:2] = 2'b00;
endmodule

module alu_sa_c (
  input  shamt,
  input  dec16,
  input  v,
  output [3:0] alu_sa_c
);


  assign alu_sa_c = {2'b00, v, dec16};
endmodule

module mgrfa3cc (
  input  r_ins,
  input  bezal,
  output o1,
  output o0
);

  wire not_1_out;

  and and_1 (o1, r_ins, bezal);
  not not_1 (not_1_out, bezal);
  and and_2 (o0, r_ins, not_1_out);
endmodule
